// Logisim project v2.circ as structural Verilog: 10 circuits, main circuit main
module main (
  input  Clock,
  input  Reset,
  output [15:0] out_3,
  output [15:0] out_4,
  output [15:0] out_5,
  output [15:0] out_6,
  output [15:0] out_7
);

  wire and_1_out, and_2_out, and_3_out, and_4_out, and_5_out, and_6_out, and_7_out, and_8_out, and_9_out,
       buffer_1_out, buffer_2_out, buffer_3_out, buffer_4_out, buffer_5_out, buffer_6_out, buffer_7_out,
       buffer_8_out, buffer_9_out, buffer_10_out, buffer_11_out, buffer_12_out, buffer_13_out, buffer_14_out,
       buffer_15_out, buffer_16_out, buffer_17_out, buffer_18_out, buffer_19_out, buffer_20_out,
       buffer_21_out, buffer_22_out, buffer_23_out, buffer_24_out, buffer_25_out, buffer_26_out,
       buffer_27_out, buffer_28_out, buffer_29_out, buffer_30_out, buffer_31_out, buffer_32_out,
       buffer_33_out, buffer_34_out, buffer_35_out, buffer_36_out, buffer_37_out, buffer_38_out,
       buffer_39_out, buffer_40_out, buffer_41_out, buffer_42_out, buffer_43_out, buffer_44_out,
       buffer_45_out, buffer_46_out, buffer_47_out, buffer_48_out, buffer_49_out, buffer_50_out,
       buffer_51_out, buffer_52_out, buffer_53_out, buffer_54_out, buffer_55_out, buffer_56_out,
       buffer_57_out, buffer_58_out, buffer_59_out, buffer_60_out, buffer_61_out, buffer_62_out,
       buffer_63_out, buffer_64_out, buffer_65_out, buffer_66_out, buffer_67_out, buffer_68_out,
       buffer_69_out, conditionaljmp_1_status, conditionaljmp_1_tock, decoder4to16_1_out_7,
       decoder4to16_1_out_8, decoder4to16_1_out_9, decoder4to16_1_out_10, decoder4to16_1_out_11,
       decoder4to16_1_out_12, decoder4to16_1_out_22, decoder4to16_1_tock, multiplexer_7_out,
       multiplexer_10_out, not_1_out, not_2_out, not_3_out, not_4_out, or_1_out, or_2_out, or_3_out,
       or_4_out, or_5_out, or_6_out, or_7_out, or_8_out, or_9_out, ReadBackTMP_tock, ReadFrom_out_7,
       ReadFrom_out_8, ReadFrom_out_9, ReadFrom_out_10, ReadFrom_out_11, ReadFrom_out_12, ReadFrom_out_13,
       ReadFrom_out_14, ReadFrom_out_15, ReadFrom_out_16, ReadFrom_out_17, ReadFrom_out_18, ReadFrom_out_19,
       ReadFrom_out_20, ReadFrom_out_21, ReadFrom_out_22, regwrap_1_tock, rise_1_out_2, rise_2_out_2,
       SendTo_out_7, SendTo_out_8, SendTo_out_9, SendTo_out_10, SendTo_out_11, SendTo_out_12, SendTo_out_13,
       SendTo_out_14, SendTo_out_15, SendTo_out_16, SendTo_out_17, SendTo_out_18, SendTo_out_19,
       SendTo_out_20, SendTo_out_21, SendTo_out_22, SendTo_tock, sp_1_tock, xor_1_out, xor_2_out;
  wire [15:0] addone_1_out_5, math_1_result, multiplexer_2_out, multiplexer_3_out, multiplexer_8_out,
       ReadBackTMP_out_7, regwrap_3_out_7, regwrap_4_out_7, regwrap_5_out_7, sp_1_out_6, sp_1_out_7;

  RAM #(.addrWidth(16), .dataWidth(16), .trigger("high")) ram_1 (
    .addr(out_3), .we(buffer_1_out), .oe(1'b1), .din(out_6), .dout(out_5));
  buf buffer_1 (buffer_1_out, buffer_2_out);
  buf buffer_2 (buffer_2_out, rise_1_out_2);
  Rise rise_1 (.in_1(and_1_out), .out_2(rise_1_out_2));
  not not_1 (not_1_out, buffer_3_out);
  buf buffer_3 (buffer_3_out, buffer_4_out);
  buf buffer_4 (buffer_4_out, buffer_5_out);
  buf buffer_5 (buffer_5_out, buffer_6_out);
  buf buffer_6 (buffer_6_out, buffer_7_out);
  buf buffer_7 (buffer_7_out, buffer_8_out);
  buf buffer_8 (buffer_8_out, buffer_9_out);
  buf buffer_9 (buffer_9_out, buffer_47_out);
  RegWrap ReadBackTMP (
    .D_in(out_5), .Tick(buffer_10_out), .Reset(Reset), .out_7(ReadBackTMP_out_7), .Tock(ReadBackTMP_tock));  // open: Write, Read, o1
  buf buffer_10 (buffer_10_out, buffer_11_out);
  buf buffer_11 (buffer_11_out, buffer_12_out);
  buf buffer_12 (buffer_12_out, buffer_13_out);
  buf buffer_13 (buffer_13_out, buffer_16_out);
  buf buffer_14 (buffer_14_out, buffer_15_out);
  buf buffer_15 (buffer_15_out, buffer_20_out);
  Multiplexer #(.width(16)) multiplexer_1 (
    .in0(addone_1_out_5), .in1(multiplexer_2_out), .out(out_3), .sel(rise_2_out_2));
  AddOne addone_1 (
    .Tick(buffer_47_out), .Overwrite(and_9_out), .Data(regwrap_5_out_7), .Reset(Reset), .out_5(addone_1_out_5));
  Multiplexer #(.width(16)) multiplexer_2 (
    .in0(regwrap_5_out_7), .in1(multiplexer_3_out), .out(multiplexer_2_out), .sel(or_2_out));
  Multiplexer #(.width(16)) multiplexer_3 (
    .in0(sp_1_out_6), .in1(sp_1_out_7), .out(multiplexer_3_out), .sel(decoder4to16_1_out_12));
  RegWrap regwrap_1 (
    .D_in(out_5), .Tick(Clock), .Reset(Reset), .out_7(out_4), .Tock(regwrap_1_tock));  // open: Write, Read, o1
  buf buffer_16 (buffer_16_out, buffer_17_out);
  buf buffer_17 (buffer_17_out, buffer_18_out);
  buf buffer_18 (buffer_18_out, buffer_19_out);
  buf buffer_19 (buffer_19_out, buffer_24_out);
  buf buffer_20 (buffer_20_out, buffer_21_out);
  buf buffer_21 (buffer_21_out, buffer_22_out);
  buf buffer_22 (buffer_22_out, buffer_23_out);
  buf buffer_23 (buffer_23_out, buffer_25_out);
  Rise rise_2 (.in_1(and_2_out), .out_2(rise_2_out_2));
  and and_1 (and_1_out, and_2_out, or_1_out);
  or or_1 (or_1_out, SendTo_out_22, decoder4to16_1_out_11);
  or or_2 (or_2_out, decoder4to16_1_out_11, decoder4to16_1_out_12);
  buf buffer_24 (buffer_24_out, buffer_14_out);
  buf buffer_25 (buffer_25_out, and_2_out);
  and and_2 (and_2_out, buffer_69_out, or_4_out);
  and and_3 (and_3_out, out_4[10], and_5_out);
  Multiplexer #(.width(16)) multiplexer_4 (.in1(sp_1_out_6), .out(out_6), .sel(and_3_out));  // open: in0
  and and_4 (and_4_out, and_5_out, out_4[11]);
  Multiplexer #(.width(16)) multiplexer_5 (.in1(addone_1_out_5), .out(out_6), .sel(and_4_out));  // open: in0
  Multiplexer #(.width(16)) multiplexer_6 (.in1(ReadBackTMP_out_7), .out(out_6), .sel(or_3_out));  // open: in0
  Multiplexer multiplexer_7 (.in0(buffer_69_out), .in1(ReadBackTMP_tock), .out(multiplexer_7_out), .sel(or_4_out));
  or or_3 (or_3_out, decoder4to16_1_out_12, ReadFrom_out_22);
  or or_4 (or_4_out, decoder4to16_1_out_11, ReadFrom_out_22, SendTo_out_22, decoder4to16_1_out_12);
  Decoder4to16 decoder4to16_1 (
    .in_1(out_4[12]), .in_2(out_4[13]), .in_3(out_4[14]), .in_4(out_4[15]), .Tick(regwrap_1_tock),
    .out_7(decoder4to16_1_out_7), .out_8(decoder4to16_1_out_8), .out_9(decoder4to16_1_out_9),
    .out_10(decoder4to16_1_out_10), .out_11(decoder4to16_1_out_11), .out_12(decoder4to16_1_out_12),
    .out_22(decoder4to16_1_out_22), .Tock(decoder4to16_1_tock));  // open: TurnOff, out_13, out_14, out_15, out_16, out_17, out_18, out_19, out_20, out_21
  buf buffer_26 (buffer_26_out, decoder4to16_1_tock);
  buf buffer_27 (buffer_27_out, and_6_out);
  and and_5 (and_5_out, decoder4to16_1_out_8, buffer_27_out);
  buf buffer_28 (buffer_28_out, buffer_27_out);
  or or_5 (or_5_out, out_4[10], out_4[11]);
  buf buffer_29 (buffer_29_out, buffer_28_out);
  not not_2 (not_2_out, decoder4to16_1_out_22);
  and and_6 (and_6_out, buffer_26_out, not_2_out);
  or or_6 (or_6_out, decoder4to16_1_out_10, decoder4to16_1_out_11, decoder4to16_1_out_8, decoder4to16_1_out_8);
  xor xor_1 (xor_1_out, or_5_out, or_6_out);
  not not_3 (not_3_out, xor_1_out);
  Decoder4to16 ReadFrom (
    .TurnOff(not_3_out), .in_1(out_4[6]), .in_2(out_4[7]), .in_3(out_4[8]), .in_4(out_4[9]),
    .Tick(buffer_29_out), .out_7(ReadFrom_out_7), .out_8(ReadFrom_out_8), .out_9(ReadFrom_out_9),
    .out_10(ReadFrom_out_10), .out_11(ReadFrom_out_11), .out_12(ReadFrom_out_12), .out_13(ReadFrom_out_13),
    .out_14(ReadFrom_out_14), .out_15(ReadFrom_out_15), .out_16(ReadFrom_out_16), .out_17(ReadFrom_out_17),
    .out_18(ReadFrom_out_18), .out_19(ReadFrom_out_19), .out_20(ReadFrom_out_20), .out_21(ReadFrom_out_21),
    .out_22(ReadFrom_out_22));  // open: Tock
  and and_7 (and_7_out, out_4[4], or_7_out, and_6_out);
  buf buffer_30 (buffer_30_out, and_6_out);
  buf buffer_31 (buffer_31_out, buffer_30_out);
  buf buffer_32 (buffer_32_out, buffer_31_out);
  xor xor_2 (xor_2_out, and_7_out, or_7_out);
  or or_7 (or_7_out, decoder4to16_1_out_8, decoder4to16_1_out_12, decoder4to16_1_out_9);
  not not_4 (not_4_out, xor_2_out);
  Decoder4to16 SendTo (
    .TurnOff(not_4_out), .in_1(out_4[0]), .in_2(out_4[1]), .in_3(out_4[2]), .in_4(out_4[3]),
    .Tick(buffer_32_out), .out_7(SendTo_out_7), .out_8(SendTo_out_8), .out_9(SendTo_out_9),
    .out_10(SendTo_out_10), .out_11(SendTo_out_11), .out_12(SendTo_out_12), .out_13(SendTo_out_13),
    .out_14(SendTo_out_14), .out_15(SendTo_out_15), .out_16(SendTo_out_16), .out_17(SendTo_out_17),
    .out_18(SendTo_out_18), .out_19(SendTo_out_19), .out_20(SendTo_out_20), .out_21(SendTo_out_21),
    .out_22(SendTo_out_22), .Tock(SendTo_tock));
  Multiplexer #(.width(16)) multiplexer_8 (
    .in0(out_6), .in1(out_4), .out(multiplexer_8_out), .sel(decoder4to16_1_out_7));
  or or_8 (or_8_out, SendTo_out_7, decoder4to16_1_out_7);
  RegWrap regwrap_2 (
    .D_in(multiplexer_8_out), .Write(or_8_out), .Read(ReadFrom_out_7), .Tick(multiplexer_10_out),
    .Reset(Reset), .o1(out_6), .out_7(out_7));  // open: Tock
  RegWrap regwrap_3 (
    .D_in(out_6), .Write(SendTo_out_8), .Read(ReadFrom_out_8), .Tick(multiplexer_10_out), .Reset(Reset),
    .o1(out_6), .out_7(regwrap_3_out_7));  // open: Tock
  RegWrap regwrap_4 (
    .D_in(out_6), .Write(SendTo_out_9), .Read(ReadFrom_out_9), .Tick(multiplexer_10_out), .Reset(Reset),
    .o1(out_6), .out_7(regwrap_4_out_7));  // open: Tock
  RegWrap regwrap_5 (
    .D_in(out_6), .Write(SendTo_out_10), .Read(ReadFrom_out_10), .Tick(multiplexer_10_out), .Reset(Reset),
    .o1(out_6), .out_7(regwrap_5_out_7));  // open: Tock
  RegWrap regwrap_6 (
    .D_in(out_6), .Write(SendTo_out_11), .Read(ReadFrom_out_11), .Tick(multiplexer_10_out), .Reset(Reset),
    .o1(out_6));  // open: out_7, Tock
  RegWrap regwrap_7 (
    .D_in(out_6), .Write(SendTo_out_12), .Read(ReadFrom_out_12), .Tick(multiplexer_10_out), .Reset(Reset),
    .o1(out_6));  // open: out_7, Tock
  RegWrap regwrap_8 (
    .D_in(out_6), .Write(SendTo_out_13), .Read(ReadFrom_out_13), .Tick(multiplexer_10_out), .Reset(Reset),
    .o1(out_6));  // open: out_7, Tock
  RegWrap regwrap_9 (
    .D_in(out_6), .Write(SendTo_out_14), .Read(ReadFrom_out_14), .Tick(multiplexer_10_out), .Reset(Reset),
    .o1(out_6));  // open: out_7, Tock
  RegWrap regwrap_10 (
    .D_in(out_6), .Write(SendTo_out_15), .Read(ReadFrom_out_15), .Tick(multiplexer_10_out), .Reset(Reset),
    .o1(out_6));  // open: out_7, Tock
  RegWrap regwrap_11 (
    .D_in(out_6), .Write(SendTo_out_16), .Read(ReadFrom_out_16), .Tick(multiplexer_10_out), .Reset(Reset),
    .o1(out_6));  // open: out_7, Tock
  RegWrap regwrap_12 (
    .D_in(out_6), .Write(SendTo_out_17), .Read(ReadFrom_out_17), .Tick(multiplexer_10_out), .Reset(Reset),
    .o1(out_6));  // open: out_7, Tock
  RegWrap regwrap_13 (
    .D_in(out_6), .Write(SendTo_out_18), .Read(ReadFrom_out_18), .Tick(multiplexer_10_out), .Reset(Reset),
    .o1(out_6));  // open: out_7, Tock
  RegWrap regwrap_14 (
    .D_in(out_6), .Write(SendTo_out_19), .Read(ReadFrom_out_19), .Tick(multiplexer_10_out), .Reset(Reset),
    .o1(out_6));  // open: out_7, Tock
  RegWrap regwrap_15 (
    .D_in(out_6), .Write(SendTo_out_20), .Read(ReadFrom_out_20), .Tick(multiplexer_10_out), .Reset(Reset),
    .o1(out_6));  // open: out_7, Tock
  RegWrap regwrap_16 (
    .D_in(out_6), .Write(SendTo_out_21), .Read(ReadFrom_out_21), .Tick(multiplexer_10_out), .Reset(Reset),
    .o1(out_6));  // open: out_7, Tock
  Multiplexer #(.width(16)) multiplexer_9 (.in1(math_1_result), .out(out_6), .sel(decoder4to16_1_out_9));  // open: in0
  or or_9 (or_9_out, decoder4to16_1_out_12, and_7_out, decoder4to16_1_out_11);
  buf buffer_33 (buffer_33_out, multiplexer_7_out);
  buf buffer_34 (buffer_34_out, buffer_33_out);
  buf buffer_35 (buffer_35_out, buffer_34_out);
  Multiplexer multiplexer_10 (.in0(buffer_35_out), .in1(buffer_38_out), .out(multiplexer_10_out), .sel(or_9_out));
  buf buffer_36 (buffer_36_out, SendTo_tock);
  buf buffer_37 (buffer_37_out, buffer_36_out);
  and and_8 (and_8_out, multiplexer_7_out, or_9_out);
  buf buffer_38 (buffer_38_out, buffer_39_out);
  buf buffer_39 (buffer_39_out, buffer_52_out);
  conditionalJmp conditionaljmp_1 (
    .Tick(buffer_40_out), .in_1(out_4[0]), .in_2(out_4[1]), .in_3(out_4[2]), .Din(out_6),
    .Status(conditionaljmp_1_status), .Tock(conditionaljmp_1_tock));
  buf buffer_40 (buffer_40_out, buffer_41_out);
  buf buffer_41 (buffer_41_out, buffer_42_out);
  buf buffer_42 (buffer_42_out, buffer_44_out);
  buf buffer_43 (buffer_43_out, conditionaljmp_1_tock);
  buf buffer_44 (buffer_44_out, multiplexer_10_out);
  buf buffer_45 (buffer_45_out, buffer_43_out);
  buf buffer_46 (buffer_46_out, buffer_45_out);
  buf buffer_47 (buffer_47_out, buffer_46_out);
  buf buffer_48 (buffer_48_out, buffer_37_out);
  buf buffer_49 (buffer_49_out, buffer_48_out);
  buf buffer_50 (buffer_50_out, buffer_49_out);
  buf buffer_51 (buffer_51_out, buffer_50_out);
  buf buffer_52 (buffer_52_out, buffer_53_out);
  buf buffer_53 (buffer_53_out, buffer_54_out);
  buf buffer_54 (buffer_54_out, buffer_55_out);
  buf buffer_55 (buffer_55_out, buffer_60_out);
  and and_9 (and_9_out, conditionaljmp_1_status, decoder4to16_1_out_10, conditionaljmp_1_tock);
  buf buffer_56 (buffer_56_out, buffer_51_out);
  buf buffer_57 (buffer_57_out, buffer_56_out);
  buf buffer_58 (buffer_58_out, buffer_57_out);
  buf buffer_59 (buffer_59_out, buffer_58_out);
  buf buffer_60 (buffer_60_out, buffer_61_out);
  buf buffer_61 (buffer_61_out, buffer_62_out);
  buf buffer_62 (buffer_62_out, buffer_63_out);
  buf buffer_63 (buffer_63_out, sp_1_tock);
  buf buffer_64 (buffer_64_out, buffer_59_out);
  buf buffer_65 (buffer_65_out, buffer_64_out);
  buf buffer_66 (buffer_66_out, buffer_65_out);
  buf buffer_67 (buffer_67_out, buffer_66_out);
  Math math_1 (
    .in_1(out_4[6]), .in_2(out_4[7]), .in_3(out_4[8]), .in_4(out_4[9]), .R1(regwrap_3_out_7),
    .R2(regwrap_4_out_7), .Result(math_1_result));
  SP sp_1 (
    .Overwrite(and_7_out), .D_in(out_6), .popping(decoder4to16_1_out_12), .Tick(and_8_out), .Reset(Reset),
    .out_6(sp_1_out_6), .out_7(sp_1_out_7), .Tock(sp_1_tock));
  buf buffer_68 (buffer_68_out, buffer_67_out);
  buf buffer_69 (buffer_69_out, buffer_68_out);

  // Notes on the sheet:
  //   On clock do
  //   1. FETCH : load instruction from ram
  //   2. DECODE : understand what the instuction said and turn some wire on and of
  //   3. EXECUTE : Do what the instruction asked 
  //   Delay 8
  //   Push or write
  //   If readback then we wait for it
  //   PC
  //   SP
  //   Check mem mod
  //   arithmatic unit : passed
  //   registers, memory : read write passed
endmodule

module Rise (
  input  in_1,
  output out_2
);

  wire not_1_out;

  not not_1 (not_1_out, in_1);
  and and_1 (out_2, in_1, not_1_out);

  // Notes on the sheet:
  //   1 Tick
endmodule

module Fall (
  input  in_1,
  output out_2
);

  wire not_1_out;

  not not_1 (not_1_out, in_1);
  nor nor_1 (out_2, not_1_out, in_1);
endmodule

module AddOne (
  input  Tick,
  input  Overwrite,
  input  [15:0] Data,
  input  Reset,
  output [15:0] out_5
);

  wire rise_1_out_2;
  wire [15:0] adder_1_out, multiplexer_1_out;

  Rise rise_1 (.in_1(Tick), .out_2(rise_1_out_2));
  Multiplexer #(.width(16)) multiplexer_1 (.in0(adder_1_out), .in1(Data), .out(multiplexer_1_out), .sel(Overwrite));
  Register #(.trigger("high"), .width(16)) register_1 (
    .D(multiplexer_1_out), .en(1'b1), .clk(rise_1_out_2), .Q(out_5), .clr(Reset));
  Adder #(.width(16)) adder_1 (.a(out_5), .b(16'h1), .out(adder_1_out));  // open: cin, cout
endmodule

module Decoder4to16 (
  input  in_1,
  input  in_2,
  input  in_3,
  input  in_4,
  input  TurnOff,
  input  Tick,
  output out_7,
  output out_8,
  output out_9,
  output out_10,
  output out_11,
  output out_12,
  output out_13,
  output out_14,
  output out_15,
  output out_16,
  output out_17,
  output out_18,
  output out_19,
  output out_20,
  output out_21,
  output out_22,
  output Tock
);

  wire buffer_1_out, buffer_2_out, buffer_3_out, buffer_4_out, buffer_5_out, buffer_6_out, buffer_7_out,
       buffer_8_out, buffer_9_out, buffer_10_out;
  wire [15:0] rom_1_data;
  wire [15:15] not_1_out;

  not not_1 (not_1_out[15], TurnOff);
  buf buffer_1 (buffer_1_out, Tick);
  buf buffer_2 (buffer_2_out, buffer_1_out);
  buf buffer_3 (buffer_3_out, buffer_2_out);
  ROM #(.addrWidth(4), .dataWidth(16)) rom_1 (.addr({in_4, in_3, in_2, in_1}), .data(rom_1_data));
  buf buffer_4 (buffer_4_out, buffer_3_out);
  buf buffer_5 (buffer_5_out, buffer_4_out);
  buf buffer_6 (buffer_6_out, buffer_5_out);
  buf buffer_7 (buffer_7_out, buffer_6_out);
  buf buffer_8 (buffer_8_out, buffer_7_out);
  buf buffer_9 (buffer_9_out, buffer_8_out);
  buf buffer_10 (buffer_10_out, buffer_9_out);
  buf buffer_11 (Tock, buffer_10_out);
  assign {out_22, out_21, out_20, out_19, out_18, out_17, out_16, out_15, out_14, out_13, out_12, out_11, out_10, out_9, out_8, out_7} = rom_1_data & {16{not_1_out[15]}};  // AND_Gate and_1, 16 bits wide

  // Notes on the sheet:
  //   TurnOff: pull=down
  //   contents of rom_1 (hex, n*v repeats v):
  //   1 2 4 8 10 20 40 80 100 200 400 800 1000 2000 4000 8000
endmodule

module RegWrap (
  input  [15:0] D_in,
  input  Write,
  input  Read,
  input  Tick,
  input  Reset,
  output [15:0] o1,
  output [15:0] out_7,
  output Tock
);

  wire and_1_out, buffer_1_out, buffer_2_out, buffer_3_out, buffer_4_out, buffer_5_out, buffer_6_out,
       buffer_8_out, buffer_9_out, buffer_10_out, multiplexer_1_out;
  wire [15:0] register_1_q;

  buf buffer_1 (buffer_1_out, Tick);
  Register #(.width(16)) register_1 (.D(D_in), .en(Write), .clk(Tick), .Q(register_1_q), .clr(Reset));
  Multiplexer multiplexer_1 (.in1(Tick), .out(multiplexer_1_out), .sel(and_1_out));  // open: in0
  and and_1 (and_1_out, Write, Read);
  buf buffer_2 (buffer_2_out, buffer_1_out);
  Multiplexer multiplexer_2 (.in0(buffer_2_out), .out(Tock), .sel(and_1_out));  // open: in1
  buf buffer_3 (buffer_3_out, multiplexer_1_out);
  buf buffer_4 (buffer_4_out, buffer_3_out);
  buf buffer_5 (buffer_5_out, buffer_4_out);
  buf buffer_6 (buffer_6_out, buffer_5_out);
  Multiplexer #(.width(16)) multiplexer_3 (.in1(register_1_q), .out(o1), .sel(Read));  // open: in0
  assign out_7 = register_1_q;  // Buffer buffer_7, 16 bits wide
  buf buffer_8 (buffer_8_out, buffer_6_out);
  buf buffer_9 (buffer_9_out, buffer_8_out);
  buf buffer_10 (buffer_10_out, buffer_9_out);
  buf buffer_11 (Tock, buffer_10_out);

  // Notes on the sheet:
  //   Write: pull=up
  //   Read: pull=up
endmodule

module Decoder6Bit (
  input  in_1,
  input  in_2,
  input  in_3,
  input  in_4,
  input  in_5,
  input  in_6,
  input  TurnOff,
  input  Tick,
  output out_9,
  output out_10,
  output out_11,
  output out_12,
  output out_13,
  output out_14,
  output out_15,
  output out_16,
  output out_17,
  output out_18,
  output out_19,
  output out_20,
  output out_21,
  output out_22,
  output out_23,
  output out_24,
  output out_25,
  output out_26,
  output out_27,
  output out_28,
  output out_29,
  output out_30,
  output out_31,
  output out_32,
  output out_33,
  output out_34,
  output out_35,
  output out_36,
  output out_37,
  output out_38,
  output out_39,
  output out_40,
  output out_41,
  output out_42,
  output out_43,
  output out_44,
  output out_45,
  output out_46,
  output out_47,
  output out_48,
  output out_49,
  output out_50,
  output out_51,
  output out_52,
  output out_53,
  output out_54,
  output out_55,
  output out_56,
  output out_57,
  output out_58,
  output out_59,
  output out_60,
  output out_61,
  output out_62,
  output out_63,
  output out_64,
  output out_65,
  output out_66,
  output out_67,
  output out_68,
  output out_69,
  output out_70,
  output out_71,
  output out_72,
  output Tock
);

  wire buffer_1_out, buffer_2_out, buffer_3_out, buffer_4_out, buffer_5_out, buffer_6_out, buffer_7_out,
       buffer_8_out, buffer_9_out, buffer_10_out;
  wire [63:0] multiplexer_1_out, rom_1_data;

  buf buffer_1 (buffer_1_out, Tick);
  buf buffer_2 (buffer_2_out, buffer_1_out);
  buf buffer_3 (buffer_3_out, buffer_2_out);
  ROM #(.addrWidth(6), .dataWidth(64)) rom_1 (.addr({in_6, in_5, in_4, in_3, in_2, in_1}), .data(rom_1_data));
  buf buffer_4 (buffer_4_out, buffer_3_out);
  buf buffer_5 (buffer_5_out, buffer_4_out);
  buf buffer_6 (buffer_6_out, buffer_5_out);
  buf buffer_7 (buffer_7_out, buffer_6_out);
  Multiplexer #(.width(64)) multiplexer_1 (.in0({64{1'b1}}), .in1({64{1'b0}}), .out(multiplexer_1_out), .sel(TurnOff));
  buf buffer_8 (buffer_8_out, buffer_7_out);
  buf buffer_9 (buffer_9_out, buffer_8_out);
  buf buffer_10 (buffer_10_out, buffer_9_out);
  buf buffer_11 (Tock, buffer_10_out);
  assign {out_72, out_71, out_70, out_69, out_68, out_67, out_66, out_65, out_64, out_63, out_62, out_61, out_60, out_59, out_58, out_57, out_56, out_55, out_54, out_53, out_52, out_51, out_50, out_49, out_48, out_47, out_46, out_45, out_44, out_43, out_42, out_41, out_40, out_39, out_38, out_37, out_36, out_35, out_34, out_33, out_32, out_31, out_30, out_29, out_28, out_27, out_26, out_25, out_24, out_23, out_22, out_21, out_20, out_19, out_18, out_17, out_16, out_15, out_14, out_13, out_12, out_11, out_10, out_9} = rom_1_data & multiplexer_1_out;  // AND_Gate and_1, 64 bits wide

  // Notes on the sheet:
  //   TurnOff: pull=down
  //   contents of rom_1 (hex, n*v repeats v):
  //   1 2 4 8 10 20 40 80 100 200 400 800 1000 2000 4000 8000 10000 20000 40000 80000 100000 200000 400000
  //   800000 1000000 2000000 4000000 8000000 10000000 20000000 40000000 80000000 100000000 200000000
  //   400000000 800000000 1000000000 2000000000 4000000000 8000000000 10000000000 20000000000 40000000000
  //   80000000000 100000000000 200000000000 400000000000 800000000000 1000000000000 2000000000000
  //   4000000000000 8000000000000 10000000000000 20000000000000 40000000000000 80000000000000
  //   100000000000000 200000000000000 400000000000000 800000000000000 1000000000000000 2000000000000000
  //   4000000000000000 8000000000000000
endmodule

module Math (
  input  in_1,
  input  in_2,
  input  in_3,
  input  in_4,
  input  [15:0] R1,
  input  [15:0] R2,
  output [15:0] Result
);

  wire decoder4to16_1_out_7, decoder4to16_1_out_8, decoder4to16_1_out_9, decoder4to16_1_out_10,
       decoder4to16_1_out_11, decoder4to16_1_out_12, decoder4to16_1_out_13, decoder4to16_1_out_14,
       decoder4to16_1_out_15, decoder4to16_1_out_16;
  wire [15:0] adder_1_out, and_1_out, divider_1_out, multiplier_1_out, not_1_out, or_1_out, shifter_1_out,
       shifter_2_out, subtractor_1_out, xor_1_out;

  Decoder4to16 decoder4to16_1 (
    .in_1(in_1), .in_2(in_2), .in_3(in_3), .in_4(in_4), .out_7(decoder4to16_1_out_7),
    .out_8(decoder4to16_1_out_8), .out_9(decoder4to16_1_out_9), .out_10(decoder4to16_1_out_10),
    .out_11(decoder4to16_1_out_11), .out_12(decoder4to16_1_out_12), .out_13(decoder4to16_1_out_13),
    .out_14(decoder4to16_1_out_14), .out_15(decoder4to16_1_out_15), .out_16(decoder4to16_1_out_16));  // open: TurnOff, Tick, out_17, out_18, out_19, out_20, out_21, out_22, Tock
  assign and_1_out = R1 & R2;  // AND_Gate and_1, 16 bits wide
  assign or_1_out = R1 | R2;  // OR_Gate or_1, 16 bits wide
  assign xor_1_out = R1 ^ R2;  // XOR_Gate xor_1, 16 bits wide
  assign not_1_out = ~R1;  // NOT_Gate not_1, 16 bits wide
  Adder #(.width(16)) adder_1 (.a(R1), .b(R2), .out(adder_1_out));  // open: cin, cout
  Subtractor #(.width(16)) subtractor_1 (.a(R1), .b(R2), .out(subtractor_1_out));  // open: bin, bout
  Multiplier #(.width(16)) multiplier_1 (.a(R1), .b(R2), .out(multiplier_1_out));  // open: cin, cout
  Divider #(.width(16)) divider_1 (.a(R1), .b(R2), .out(divider_1_out));  // open: upper, rem
  Shifter #(.width(16)) shifter_1 (.in(R1), .\dist (R2[3:0]), .out(shifter_1_out));
  Shifter #(.shift("lr"), .width(16)) shifter_2 (.in(R1), .\dist (R2[3:0]), .out(shifter_2_out));
  Multiplexer #(.width(16)) multiplexer_1 (.in1(and_1_out), .out(Result), .sel(decoder4to16_1_out_7));  // open: in0
  Multiplexer #(.width(16)) multiplexer_2 (.in1(or_1_out), .out(Result), .sel(decoder4to16_1_out_8));  // open: in0
  Multiplexer #(.width(16)) multiplexer_3 (.in1(xor_1_out), .out(Result), .sel(decoder4to16_1_out_9));  // open: in0
  Multiplexer #(.width(16)) multiplexer_4 (.in1(not_1_out), .out(Result), .sel(decoder4to16_1_out_10));  // open: in0
  Multiplexer #(.width(16)) multiplexer_5 (.in1(adder_1_out), .out(Result), .sel(decoder4to16_1_out_11));  // open: in0
  Multiplexer #(.width(16)) multiplexer_6 (
    .in1(subtractor_1_out), .out(Result), .sel(decoder4to16_1_out_12));  // open: in0
  Multiplexer #(.width(16)) multiplexer_7 (
    .in1(multiplier_1_out), .out(Result), .sel(decoder4to16_1_out_13));  // open: in0
  Multiplexer #(.width(16)) multiplexer_8 (
    .in1(divider_1_out), .out(Result), .sel(decoder4to16_1_out_14));  // open: in0
  Multiplexer #(.width(16)) multiplexer_9 (
    .in1(shifter_1_out), .out(Result), .sel(decoder4to16_1_out_15));  // open: in0
  Multiplexer #(.width(16)) multiplexer_10 (
    .in1(shifter_2_out), .out(Result), .sel(decoder4to16_1_out_16));  // open: in0
endmodule

module SP (
  input  Overwrite,
  input  [15:0] D_in,
  input  popping,
  input  Tick,
  input  Reset,
  output [15:0] out_6,
  output [15:0] out_7,
  output Tock
);

  wire [15:0] adder_1_out, multiplexer_1_out, multiplexer_2_out, not_1_out, regwrap_1_out_7, subtractor_1_out;

  assign not_1_out = ~D_in;  // NOT_Gate not_1, 16 bits wide
  RegWrap regwrap_1 (
    .D_in(multiplexer_1_out), .Tick(Tick), .Reset(Reset), .out_7(regwrap_1_out_7), .Tock(Tock));  // open: Write, Read, o1
  Multiplexer #(.width(16)) multiplexer_1 (
    .in0(multiplexer_2_out), .in1(not_1_out), .out(multiplexer_1_out), .sel(Overwrite));
  Adder #(.width(16)) adder_1 (.a(regwrap_1_out_7), .b(16'h1), .out(adder_1_out));  // open: cin, cout
  Subtractor #(.width(16)) subtractor_1 (.a(regwrap_1_out_7), .b(16'h1), .out(subtractor_1_out));  // open: bin, bout
  Multiplexer #(.width(16)) multiplexer_2 (
    .in0(adder_1_out), .in1(subtractor_1_out), .out(multiplexer_2_out), .sel(popping));
  assign out_6 = ~regwrap_1_out_7;  // NOT_Gate not_2, 16 bits wide
  assign out_7 = ~subtractor_1_out;  // NOT_Gate not_3, 16 bits wide
endmodule

module conditionalJmp (
  input  in_1,
  input  in_2,
  input  in_3,
  input  [15:0] Din,
  input  Tick,
  output Status,
  output Tock
);

  wire and_1_out, and_2_out, buffer_1_out, buffer_2_out, buffer_3_out, nor_1_out, or_1_out;

  buf buffer_1 (buffer_1_out, Tick);
  buf buffer_2 (buffer_2_out, buffer_1_out);
  buf buffer_3 (buffer_3_out, buffer_2_out);
  and and_1 (and_1_out, in_2, Din[15]);
  and and_2 (and_2_out, in_1, nor_1_out);
  nor nor_1 (nor_1_out, Din[0], Din[1], Din[2], Din[3], Din[4], Din[5], Din[6], Din[7], Din[8], Din[9], Din[10], Din[11], Din[12], Din[13], Din[14], Din[15]);
  buf buffer_4 (Tock, buffer_3_out);
  or or_1 (or_1_out, and_1_out, and_2_out);
  xor xor_1 (Status, or_1_out, in_3);
endmodule
