// Logisim project yeah.circ as structural Verilog: 11 circuits, main circuit main
module main (
  input  in_1,
  input  Reset,
  output [15:0] out_3,
  output [15:0] out_4,
  output [15:0] out_5,
  output [15:0] out_6,
  output [15:0] out_7,
  output [15:0] out_8,
  output [15:0] out_9
);

  wire and_1_out, and_2_out, and_3_out, and_4_out, and_5_out, and_6_out, and_7_out, and_8_out, and_9_out,
       and_10_out, and_11_out, buffer_1_out, buffer_2_out, buffer_3_out, buffer_4_out, buffer_5_out,
       buffer_6_out, buffer_7_out, buffer_8_out, buffer_9_out, buffer_10_out, buffer_11_out, buffer_12_out,
       buffer_13_out, buffer_14_out, buffer_15_out, buffer_16_out, buffer_17_out, buffer_18_out,
       buffer_19_out, buffer_20_out, buffer_21_out, buffer_22_out, buffer_23_out, buffer_24_out,
       buffer_25_out, buffer_26_out, buffer_27_out, buffer_28_out, buffer_29_out, buffer_30_out,
       buffer_31_out, buffer_32_out, buffer_33_out, buffer_34_out, buffer_35_out, buffer_36_out,
       buffer_37_out, buffer_38_out, buffer_39_out, buffer_40_out, buffer_41_out, buffer_42_out,
       buffer_43_out, buffer_44_out, buffer_45_out, condition_1_finish, condition_1_result,
       decoder_4bto16_1_out_6, decoder_4bto16_1_out_7, decoder_4bto16_1_out_8, decoder_4bto16_1_out_9,
       decoder_4bto16_1_out_10, decoder_4bto16_1_out_11, DTo_out_6, DTo_out_7, DTo_out_8, DTo_out_9,
       DTo_out_10, DTo_out_11, DTo_out_12, DTo_out_13, DTo_out_14, DTo_out_15, DTo_out_16, DTo_out_17,
       DTo_out_18, DTo_out_19, DTo_out_20, DTo_out_21, From_out_6, From_out_7, From_out_8, From_out_9,
       From_out_10, From_out_11, From_out_12, From_out_13, From_out_14, From_out_15, From_out_16,
       From_out_17, From_out_18, From_out_19, From_out_20, From_out_21, nor_1_out, not_1_out, not_2_out,
       not_3_out, not_4_out, not_5_out, not_6_out, not_7_out, not_8_out, not_9_out, not_10_out, not_11_out,
       not_12_out, not_13_out, not_14_out, or_1_out, or_2_out, or_3_out, or_4_out, or_5_out, or_6_out,
       or_7_out, or_8_out, or_9_out, rise_edge_1_out_2, rise_edge_2_out_2, xor_1_out;
  wire [15:0] adder_1_out, addone_1_out_5, math_1_out_5, multiplexer_6_out, multiplexer_7_out,
       multiplexer_9_out, not_16_out, register_1_q, register_3_q, regwrap_2_out_7, regwrap_3_out_7,
       regwrap_4_out_7, subtractor_1_out;

  RAM #(.addrWidth(16), .dataWidth(16), .trigger("high")) ram_1 (
    .addr(out_5), .we(rise_edge_1_out_2), .oe(1'b1), .din(out_7), .dout(out_6));
  Rise_Edge rise_edge_1 (.in_1(buffer_1_out), .out_2(rise_edge_1_out_2));
  buf buffer_1 (buffer_1_out, buffer_2_out);
  buf buffer_2 (buffer_2_out, or_1_out);
  or or_1 (or_1_out, and_2_out, buffer_3_out);
  buf buffer_3 (buffer_3_out, buffer_4_out);
  buf buffer_4 (buffer_4_out, buffer_28_out);
  or or_2 (or_2_out, and_4_out, buffer_10_out);
  buf buffer_5 (buffer_5_out, buffer_19_out);
  buf buffer_6 (buffer_6_out, buffer_5_out);
  buf buffer_7 (buffer_7_out, buffer_6_out);
  buf buffer_8 (buffer_8_out, or_2_out);
  buf buffer_9 (buffer_9_out, buffer_8_out);
  buf buffer_10 (buffer_10_out, buffer_20_out);
  Multiplexer #(.width(16)) multiplexer_1 (.in1(multiplexer_9_out), .out(out_5), .sel(buffer_10_out));  // open: in0
  buf buffer_11 (buffer_11_out, and_4_out);
  Multiplexer #(.width(16)) multiplexer_2 (.in1(regwrap_4_out_7), .out(out_5), .sel(buffer_11_out));  // open: in0
  nor nor_1 (nor_1_out, buffer_10_out, and_4_out);
  Multiplexer #(.width(16)) multiplexer_3 (.in1(addone_1_out_5), .out(out_5), .sel(nor_1_out));  // open: in0
  buf buffer_12 (buffer_12_out, buffer_7_out);
  buf buffer_13 (buffer_13_out, buffer_12_out);
  buf buffer_14 (buffer_14_out, buffer_13_out);
  buf buffer_15 (buffer_15_out, buffer_14_out);
  buf buffer_16 (buffer_16_out, buffer_9_out);
  buf buffer_17 (buffer_17_out, buffer_16_out);
  buf buffer_18 (buffer_18_out, buffer_17_out);
  buf buffer_19 (buffer_19_out, buffer_18_out);
  and and_1 (and_1_out, in_1, not_1_out);
  and and_2 (and_2_out, decoder_4bto16_1_out_10, buffer_21_out);
  buf buffer_20 (buffer_20_out, buffer_21_out);
  buf buffer_21 (buffer_21_out, buffer_22_out);
  buf buffer_22 (buffer_22_out, buffer_23_out);
  AddOne addone_1 (
    .Tick(and_1_out), .Overwrite(and_11_out), .Data(regwrap_4_out_7), .Reset(Reset), .out_5(addone_1_out_5));  // open: out_6
  Multiplexer #(.width(16)) multiplexer_4 (.in1(addone_1_out_5), .out(out_7), .sel(and_6_out));  // open: in0
  and and_3 (and_3_out, out_4[15], out_4[14], out_4[13], out_4[12], out_4[11], out_4[10], out_4[9], out_4[8], out_4[7], out_4[6], out_4[5], out_4[4], out_4[3], out_4[2], out_4[1], out_4[0]);
  not not_1 (not_1_out, and_3_out);
  Register #(.width(16)) register_1 (.D(out_6), .Q(register_1_q), .clk(buffer_15_out), .clr(Reset));  // open: en
  buf buffer_23 (buffer_23_out, buffer_24_out);
  buf buffer_24 (buffer_24_out, buffer_25_out);
  buf buffer_25 (buffer_25_out, buffer_26_out);
  buf buffer_26 (buffer_26_out, buffer_27_out);
  xor xor_1 (xor_1_out, or_3_out, buffer_28_out);
  and and_4 (and_4_out, not_3_out, xor_1_out);
  Register #(.trigger("falling"), .width(16)) register_2 (
    .D(out_6), .clk(or_4_out), .Q(out_4), .clr(Reset));  // open: en
  buf or_3 (or_3_out, From_out_21);  // OR_Gate
  Multiplexer #(.width(16)) multiplexer_5 (
    .in1(register_1_q), .out(out_7), .sel(decoder_4bto16_1_out_11));  // open: in0
  or or_4 (or_4_out, and_11_out, and_1_out);
  not not_2 (not_2_out, not_6_out);
  buf buffer_27 (buffer_27_out, and_5_out);
  and and_5 (and_5_out, not_2_out, buffer_37_out);
  buf buffer_28 (buffer_28_out, buffer_29_out);
  buf buffer_29 (buffer_29_out, buffer_30_out);
  buf buffer_30 (buffer_30_out, buffer_38_out);
  not not_3 (not_3_out, not_4_out);
  not not_4 (not_4_out, not_5_out);
  not not_5 (not_5_out, xor_1_out);
  or or_5 (or_5_out, buffer_10_out, buffer_31_out);
  buf buffer_31 (buffer_31_out, buffer_32_out);
  buf buffer_32 (buffer_32_out, buffer_33_out);
  buf buffer_33 (buffer_33_out, buffer_40_out);
  buf buffer_34 (buffer_34_out, buffer_35_out);
  buf buffer_35 (buffer_35_out, buffer_36_out);
  buf buffer_36 (buffer_36_out, buffer_42_out);
  and and_6 (and_6_out, not_8_out, out_4[10]);
  or or_6 (or_6_out, decoder_4bto16_1_out_11, decoder_4bto16_1_out_10);
  buf buffer_37 (buffer_37_out, or_6_out);
  not not_6 (not_6_out, not_7_out);
  not not_7 (not_7_out, buffer_37_out);
  buf buffer_38 (buffer_38_out, buffer_39_out);
  buf buffer_39 (buffer_39_out, DTo_out_21);
  buf buffer_40 (buffer_40_out, buffer_41_out);
  buf buffer_41 (buffer_41_out, buffer_34_out);
  buf buffer_42 (buffer_42_out, buffer_43_out);
  buf buffer_43 (buffer_43_out, and_8_out);
  not not_8 (not_8_out, and_3_out);
  and and_7 (and_7_out, not_10_out, not_12_out, not_11_out);
  or or_7 (or_7_out, out_4[10], out_4[11], and_7_out);
  and and_8 (and_8_out, and_1_out, rise_edge_2_out_2);
  Rise_Edge rise_edge_2 (.in_1(decoder_4bto16_1_out_10), .out_2(rise_edge_2_out_2));
  decoder_4bTo16 From (
    .in_1(out_4[6]), .in_2(out_4[7]), .in_3(out_4[8]), .in_4(out_4[9]), .Disabled(or_7_out),
    .out_6(From_out_6), .out_7(From_out_7), .out_8(From_out_8), .out_9(From_out_9), .out_10(From_out_10),
    .out_11(From_out_11), .out_12(From_out_12), .out_13(From_out_13), .out_14(From_out_14),
    .out_15(From_out_15), .out_16(From_out_16), .out_17(From_out_17), .out_18(From_out_18),
    .out_19(From_out_19), .out_20(From_out_20), .out_21(From_out_21));
  or or_8 (or_8_out, and_9_out, and_3_out);
  decoder_4bTo16 decoder_4bto16_1 (
    .in_1(out_4[12]), .in_2(out_4[13]), .in_3(out_4[14]), .in_4(out_4[15]), .out_6(decoder_4bto16_1_out_6),
    .out_7(decoder_4bto16_1_out_7), .out_8(decoder_4bto16_1_out_8), .out_9(decoder_4bto16_1_out_9),
    .out_10(decoder_4bto16_1_out_10), .out_11(decoder_4bto16_1_out_11));  // open: Disabled, out_12, out_13, out_14, out_15, out_16, out_17, out_18, out_19, out_20, out_21
  not not_9 (not_9_out, decoder_4bto16_1_out_11);
  not not_10 (not_10_out, decoder_4bto16_1_out_10);
  and and_9 (and_9_out, not_11_out, not_13_out, not_9_out);
  not not_11 (not_11_out, decoder_4bto16_1_out_7);
  not not_12 (not_12_out, decoder_4bto16_1_out_9);
  not not_13 (not_13_out, decoder_4bto16_1_out_8);
  decoder_4bTo16 DTo (
    .in_1(out_4[0]), .in_2(out_4[1]), .in_3(out_4[2]), .in_4(out_4[3]), .Disabled(or_8_out),
    .out_6(DTo_out_6), .out_7(DTo_out_7), .out_8(DTo_out_8), .out_9(DTo_out_9), .out_10(DTo_out_10),
    .out_11(DTo_out_11), .out_12(DTo_out_12), .out_13(DTo_out_13), .out_14(DTo_out_14), .out_15(DTo_out_15),
    .out_16(DTo_out_16), .out_17(DTo_out_17), .out_18(DTo_out_18), .out_19(DTo_out_19), .out_20(DTo_out_20),
    .out_21(DTo_out_21));
  or or_9 (or_9_out, decoder_4bto16_1_out_6, DTo_out_6);
  Multiplexer #(.width(16)) multiplexer_6 (
    .in0(out_7), .in1(out_4), .out(multiplexer_6_out), .sel(decoder_4bto16_1_out_6));
  not not_14 (not_14_out, and_3_out);
  and and_10 (and_10_out, not_14_out, out_4[11]);
  regwrap regwrap_1 (
    .Write(or_9_out), .clck(and_1_out), .D_in(multiplexer_6_out), .Reset(Reset), .Read(From_out_6),
    .out_6(out_7));  // open: out_7
  regwrap regwrap_2 (
    .Write(DTo_out_7), .clck(and_1_out), .D_in(out_7), .Reset(Reset), .Read(From_out_7), .out_6(out_7),
    .out_7(regwrap_2_out_7));
  regwrap regwrap_3 (
    .Write(DTo_out_8), .clck(and_1_out), .D_in(out_7), .Reset(Reset), .Read(From_out_8), .out_6(out_7),
    .out_7(regwrap_3_out_7));
  regwrap regwrap_4 (
    .Write(DTo_out_9), .clck(and_1_out), .D_in(out_7), .Reset(Reset), .Read(From_out_9), .out_6(out_7),
    .out_7(regwrap_4_out_7));
  regwrap regwrap_5 (
    .Write(DTo_out_10), .clck(and_1_out), .D_in(out_7), .Reset(Reset), .Read(From_out_10), .out_6(out_7));  // open: out_7
  regwrap regwrap_6 (
    .Write(DTo_out_11), .clck(and_1_out), .D_in(out_7), .Reset(Reset), .Read(From_out_11), .out_6(out_7));  // open: out_7
  regwrap regwrap_7 (
    .Write(DTo_out_12), .clck(and_1_out), .D_in(out_7), .Reset(Reset), .Read(From_out_12), .out_6(out_7));  // open: out_7
  regwrap regwrap_8 (
    .Write(DTo_out_13), .clck(and_1_out), .D_in(out_7), .Reset(Reset), .Read(From_out_13), .out_6(out_7));  // open: out_7
  regwrap regwrap_9 (
    .Write(DTo_out_14), .clck(and_1_out), .D_in(out_7), .Reset(Reset), .Read(From_out_14), .out_6(out_7));  // open: out_7
  regwrap regwrap_10 (
    .Write(DTo_out_15), .clck(and_1_out), .D_in(out_7), .Reset(Reset), .Read(From_out_15), .out_6(out_7));  // open: out_7
  regwrap regwrap_11 (
    .Write(DTo_out_16), .clck(and_1_out), .D_in(out_7), .Reset(Reset), .Read(From_out_16), .out_6(out_7));  // open: out_7
  regwrap regwrap_12 (
    .Write(DTo_out_17), .clck(and_1_out), .D_in(out_7), .Reset(Reset), .Read(From_out_17), .out_6(out_7));  // open: out_7
  regwrap regwrap_13 (
    .Write(DTo_out_18), .clck(and_1_out), .D_in(out_7), .Reset(Reset), .Read(From_out_18), .out_6(out_7));  // open: out_7
  regwrap regwrap_14 (
    .Write(DTo_out_19), .clck(and_1_out), .D_in(out_7), .Reset(Reset), .Read(From_out_19), .out_6(out_7));  // open: out_7
  regwrap regwrap_15 (
    .Write(DTo_out_20), .clck(and_1_out), .D_in(out_7), .Reset(Reset), .Read(From_out_20), .out_6(out_7));  // open: out_7
  Register #(.width(16)) register_3 (.D(multiplexer_7_out), .Q(register_3_q), .clk(or_5_out), .clr(Reset));  // open: en
  assign out_3 = ~register_3_q;  // NOT_Gate not_15, 16 bits wide
  Multiplexer #(.width(16)) multiplexer_7 (
    .in0(adder_1_out), .in1(subtractor_1_out), .out(multiplexer_7_out), .sel(decoder_4bto16_1_out_11));
  buf buffer_44 (buffer_44_out, and_1_out);
  buf buffer_45 (buffer_45_out, buffer_44_out);
  Adder #(.width(16)) adder_1 (.a(register_3_q), .b(16'h1), .out(adder_1_out));  // open: cin, cout
  Subtractor #(.width(16)) subtractor_1 (.a(register_3_q), .b(16'h1), .out(subtractor_1_out));  // open: bin, bout
  Multiplexer #(.width(16)) multiplexer_8 (.in1(multiplexer_9_out), .out(out_7), .sel(and_10_out));  // open: in0
  assign not_16_out = ~subtractor_1_out;  // NOT_Gate not_16, 16 bits wide
  Multiplexer #(.width(16)) multiplexer_9 (
    .in0(out_3), .in1(not_16_out), .out(multiplexer_9_out), .sel(decoder_4bto16_1_out_11));
  Multiplexer #(.width(16)) multiplexer_10 (
    .in1(math_1_out_5), .out(out_7), .sel(decoder_4bto16_1_out_8));  // open: in0
  Condition condition_1 (
    .Clock(buffer_45_out), .Cond(out_4), .Data(out_7), .Result(condition_1_result),
    .Finish(condition_1_finish));
  and and_11 (and_11_out, condition_1_result, decoder_4bto16_1_out_9, condition_1_finish);
  Math math_1 (.OPcode(out_4), .R1(regwrap_2_out_7), .R2(regwrap_3_out_7), .Clock(and_1_out), .out_5(math_1_out_5));

  assign out_8 = out_7;
  assign out_9 = out_7;

  // Notes on the sheet:
  //   Stack pointer handler thingey yay
endmodule

module TriRead (
  input  [15:0] D_in,
  input  ReadSig,
  output [15:0] out_3,
  output [15:0] out_4
);

  Multiplexer #(.width(16)) multiplexer_1 (.in1(D_in), .out(out_3), .sel(ReadSig));  // open: in0

  assign out_4 = D_in;
endmodule

module decoder_4bTo16 (
  input  in_1,
  input  in_2,
  input  in_3,
  input  in_4,
  input  Disabled,
  output out_6,
  output out_7,
  output out_8,
  output out_9,
  output out_10,
  output out_11,
  output out_12,
  output out_13,
  output out_14,
  output out_15,
  output out_16,
  output out_17,
  output out_18,
  output out_19,
  output out_20,
  output out_21
);

  wire [15:0] rom_1_data;
  wire [15:15] not_1_out;

  Pull_Resistor pull_resistor_1 (.node(in_4));
  Pull_Resistor pull_resistor_2 (.node(in_3));
  Pull_Resistor pull_resistor_3 (.node(in_2));
  not not_1 (not_1_out[15], Disabled);
  Pull_Resistor pull_resistor_4 (.node(not_1_out[15]));
  Pull_Resistor pull_resistor_5 (.node(in_1));
  ROM #(.addrWidth(4), .dataWidth(16)) rom_1 (.addr({in_4, in_3, in_2, in_1}), .data(rom_1_data));
  assign {out_21, out_20, out_19, out_18, out_17, out_16, out_15, out_14, out_13, out_12, out_11, out_10, out_9, out_8, out_7, out_6} = rom_1_data & {16{not_1_out[15]}};  // AND_Gate and_1, 16 bits wide

  // Notes on the sheet:
  //   contents of rom_1 (hex, n*v repeats v):
  //   1 2 4 8 10 20 40 80 100 200 400 800 1000 2000 4000 8000
endmodule

module small3And (
  input  in_1,
  input  in_2,
  input  in_3,
  output out_4,
  output out_5
);

  and and_1 (out_4, in_1, in_2, in_3);
  and and_2 (out_5, in_1, in_2);
endmodule

module regwrap (
  input  Write,
  input  [15:0] D_in,
  input  Read,
  input  clck,
  input  Reset,
  output [15:0] out_6,
  output [15:0] out_7
);

  wire [15:0] register_1_q;

  Register #(.trigger("high"), .width(16)) register_1 (.D(D_in), .en(Write), .clk(clck), .Q(register_1_q), .clr(Reset));
  Pull_Resistor pull_resistor_1 (.node(Reset));
  TriRead triread_1 (.D_in(register_1_q), .ReadSig(Read), .out_3(out_6), .out_4(out_7));
endmodule

module Rise_Edge (
  input  in_1,
  output out_2
);

  wire not_1_out;

  not not_1 (not_1_out, in_1);
  and and_1 (out_2, not_1_out, in_1);
endmodule

module AddOne (
  input  Tick,
  input  Overwrite,
  input  [15:0] Data,
  input  Reset,
  output [15:0] out_5,
  output [15:0] out_6
);

  wire buffer_1_out, fall_edge_1_out_2, or_1_out, rise_edge_1_out_2;
  wire [15:0] adder_1_out, multiplexer_1_out;

  Rise_Edge rise_edge_1 (.in_1(Overwrite), .out_2(rise_edge_1_out_2));
  Fall_Edge fall_edge_1 (.in_1(Tick), .out_2(fall_edge_1_out_2));
  buf buffer_1 (buffer_1_out, rise_edge_1_out_2);
  or or_1 (or_1_out, fall_edge_1_out_2, buffer_1_out);
  Register #(.trigger("falling"), .width(16)) register_1 (
    .D(multiplexer_1_out), .en(1'b1), .clk(or_1_out), .Q(out_5), .clr(Reset));
  Multiplexer #(.width(16)) multiplexer_1 (
    .in0(adder_1_out), .in1(Data), .out(multiplexer_1_out), .sel(rise_edge_1_out_2));
  Adder #(.width(16)) adder_1 (.a(out_5), .b(16'h1), .out(adder_1_out));  // open: cin, cout
  Subtractor #(.width(16)) subtractor_1 (.a(out_5), .b(16'h1), .out(out_6));  // open: bin, bout

  // Notes on the sheet:
  //   Overwrite: pull=down
  //   Reset: pull=down
endmodule

module Fall_Edge (
  input  in_1,
  output out_2
);

  wire not_1_out;

  not not_1 (not_1_out, in_1);
  nor nor_1 (out_2, not_1_out, in_1);
endmodule

module Edging (
  input  in_1,
  output out_2
);

  wire buffer_1_out;

  buf buffer_1 (buffer_1_out, in_1);
  xor xor_1 (out_2, buffer_1_out, in_1);
endmodule

module Math (
  input  [15:0] OPcode,
  input  [15:0] R1,
  input  [15:0] R2,
  input  Clock,
  output [15:0] out_5
);

  wire buffer_1_out, decoder_4bto16_1_out_6, decoder_4bto16_1_out_7, decoder_4bto16_1_out_8,
       decoder_4bto16_1_out_9, decoder_4bto16_1_out_10, decoder_4bto16_1_out_11, decoder_4bto16_1_out_12,
       decoder_4bto16_1_out_13, decoder_4bto16_1_out_14, decoder_4bto16_1_out_15, not_1_out;
  wire [15:0] adder_1_out, and_1_out, divider_1_out, multiplexer_1_out, multiplier_1_out, not_2_out,
       or_1_out, shifter_1_out, shifter_2_out, subtractor_1_out, xor_1_out;

  decoder_4bTo16 decoder_4bto16_1 (
    .in_1(OPcode[6]), .in_2(OPcode[7]), .in_3(OPcode[8]), .in_4(OPcode[9]), .out_6(decoder_4bto16_1_out_6),
    .out_7(decoder_4bto16_1_out_7), .out_8(decoder_4bto16_1_out_8), .out_9(decoder_4bto16_1_out_9),
    .out_10(decoder_4bto16_1_out_10), .out_11(decoder_4bto16_1_out_11), .out_12(decoder_4bto16_1_out_12),
    .out_13(decoder_4bto16_1_out_13), .out_14(decoder_4bto16_1_out_14), .out_15(decoder_4bto16_1_out_15));  // open: Disabled, out_16, out_17, out_18, out_19, out_20, out_21
  Shifter #(.width(16)) shifter_1 (.in(R1), .\dist (R2[3:0]), .out(shifter_1_out));
  Shifter #(.shift("lr"), .width(16)) shifter_2 (.in(R1), .\dist (R2[3:0]), .out(shifter_2_out));
  Register #(.width(16)) register_1 (
    .D(multiplexer_1_out), .clk(buffer_1_out), .Q(out_5), .clr(not_1_out));  // open: en
  buf buffer_1 (buffer_1_out, Clock);
  not not_1 (not_1_out, Clock);
  Multiplexer #(.width(16)) multiplexer_1 (
    .in1(and_1_out), .out(multiplexer_1_out), .sel(decoder_4bto16_1_out_6));  // open: in0
  assign and_1_out = R1 & R2;  // AND_Gate and_1, 16 bits wide
  Multiplexer #(.width(16)) multiplexer_2 (
    .in1(or_1_out), .out(multiplexer_1_out), .sel(decoder_4bto16_1_out_7));  // open: in0
  assign or_1_out = R1 | R2;  // OR_Gate or_1, 16 bits wide
  Multiplexer #(.width(16)) multiplexer_3 (
    .in1(xor_1_out), .out(multiplexer_1_out), .sel(decoder_4bto16_1_out_8));  // open: in0
  assign xor_1_out = R1 ^ R2;  // XOR_Gate xor_1, 16 bits wide
  Multiplexer #(.width(16)) multiplexer_4 (
    .in1(not_2_out), .out(multiplexer_1_out), .sel(decoder_4bto16_1_out_9));  // open: in0
  assign not_2_out = ~R1;  // NOT_Gate not_2, 16 bits wide
  Multiplexer #(.width(16)) multiplexer_5 (
    .in1(adder_1_out), .out(multiplexer_1_out), .sel(decoder_4bto16_1_out_10));  // open: in0
  Adder #(.width(16)) adder_1 (.a(R1), .b(R2), .out(adder_1_out));  // open: cin, cout
  Multiplexer #(.width(16)) multiplexer_6 (
    .in1(subtractor_1_out), .out(multiplexer_1_out), .sel(decoder_4bto16_1_out_11));  // open: in0
  Subtractor #(.width(16)) subtractor_1 (.a(R1), .b(R2), .out(subtractor_1_out));  // open: bin, bout
  Multiplexer #(.width(16)) multiplexer_7 (
    .in1(multiplier_1_out), .out(multiplexer_1_out), .sel(decoder_4bto16_1_out_12));  // open: in0
  Multiplier #(.width(16)) multiplier_1 (.a(R1), .b(R2), .out(multiplier_1_out));  // open: cin, cout
  Multiplexer #(.width(16)) multiplexer_8 (
    .in1(divider_1_out), .out(multiplexer_1_out), .sel(decoder_4bto16_1_out_13));  // open: in0
  Divider #(.width(16)) divider_1 (.a(R1), .b(R2), .out(divider_1_out));  // open: upper, rem
  Multiplexer #(.width(16)) multiplexer_9 (
    .in1(shifter_1_out), .out(multiplexer_1_out), .sel(decoder_4bto16_1_out_14));  // open: in0
  Multiplexer #(.width(16)) multiplexer_10 (
    .in1(shifter_2_out), .out(multiplexer_1_out), .sel(decoder_4bto16_1_out_15));  // open: in0

  // Notes on the sheet:
  //   out_5: pull=down
endmodule

module Condition (
  input  [15:0] Cond,
  input  [15:0] Data,
  input  Clock,
  output Result,
  output Finish
);

  wire and_1_out, buffer_1_out, buffer_2_out, buffer_3_out, buffer_4_out, buffer_5_out,
       decoder_4bto16_1_out_6, decoder_4bto16_1_out_7, decoder_4bto16_1_out_8, decoder_4bto16_1_out_9,
       decoder_4bto16_1_out_10, decoder_4bto16_1_out_11, decoder_4bto16_1_out_12, decoder_4bto16_1_out_13,
       nor_1_out, not_1_out, not_2_out, or_1_out;

  buf buffer_1 (buffer_1_out, Clock);
  buf buffer_2 (buffer_2_out, buffer_1_out);
  buf buffer_3 (buffer_3_out, buffer_2_out);
  buf buffer_4 (buffer_4_out, buffer_3_out);
  buf buffer_5 (buffer_5_out, buffer_4_out);
  buf buffer_6 (Finish, buffer_5_out);
  decoder_4bTo16 decoder_4bto16_1 (
    .in_1(Cond[6]), .in_2(Cond[7]), .in_3(Cond[8]), .out_6(decoder_4bto16_1_out_6),
    .out_7(decoder_4bto16_1_out_7), .out_8(decoder_4bto16_1_out_8), .out_9(decoder_4bto16_1_out_9),
    .out_10(decoder_4bto16_1_out_10), .out_11(decoder_4bto16_1_out_11), .out_12(decoder_4bto16_1_out_12),
    .out_13(decoder_4bto16_1_out_13));  // open: in_4, Disabled, out_14, out_15, out_16, out_17, out_18, out_19, out_20, out_21
  nor nor_1 (nor_1_out, Data[0], Data[1], Data[2], Data[3], Data[4], Data[5], Data[6], Data[7], Data[8], Data[9], Data[10], Data[11], Data[12], Data[13], Data[14], Data[15]);
  or or_1 (or_1_out, Data[15], nor_1_out);
  not not_1 (not_1_out, nor_1_out);
  not not_2 (not_2_out, Data[15]);
  and and_1 (and_1_out, not_1_out, not_2_out);
  Multiplexer multiplexer_1 (.in1(1'b1), .out(Result), .sel(decoder_4bto16_1_out_6));  // open: in0
  Multiplexer multiplexer_2 (.in1(1'b0), .out(Result), .sel(decoder_4bto16_1_out_7));  // open: in0
  Multiplexer multiplexer_3 (.in1(nor_1_out), .out(Result), .sel(decoder_4bto16_1_out_8));  // open: in0
  Multiplexer multiplexer_4 (.in1(not_1_out), .out(Result), .sel(decoder_4bto16_1_out_9));  // open: in0
  Multiplexer multiplexer_5 (.in1(and_1_out), .out(Result), .sel(decoder_4bto16_1_out_10));  // open: in0
  Multiplexer multiplexer_6 (.in1(Data[15]), .out(Result), .sel(decoder_4bto16_1_out_11));  // open: in0
  Multiplexer multiplexer_7 (.in1(not_2_out), .sel(decoder_4bto16_1_out_12));  // open: in0, out
  Multiplexer multiplexer_8 (.in1(or_1_out), .sel(decoder_4bto16_1_out_13));  // open: in0, out
endmodule
