// Logisim project conputer.circ as structural Verilog: 9 circuits, main circuit main
module main (
  input  Reset,
  output [7:0] out_2,
  output [7:0] out_3,
  output [7:0] out_4,
  output [7:0] out_5,
  output [7:0] out_6
);

  wire and_1_out, buffer_1_out, buffer_2_out, buffer_3_out, buffer_4_out, buffer_5_out, buffer_6_out,
       buffer_7_out, buffer_8_out, buffer_9_out, buffer_10_out, buffer_11_out, buffer_12_out, buffer_13_out,
       buffer_14_out, buffer_15_out, buffer_16_out, buffer_17_out, buffer_18_out, buffer_19_out,
       buffer_20_out, buffer_21_out, buffer_22_out, buffer_23_out, buffer_24_out, buffer_25_out,
       buffer_26_out, buffer_27_out, buffer_28_out, buffer_29_out, buffer_30_out, buffer_31_out,
       buffer_32_out, buffer_33_out, buffer_34_out, buffer_35_out, buffer_36_out, buffer_37_out,
       buffer_38_out, buffer_39_out, buffer_40_out, buffer_41_out, buffer_42_out, clock_1_out,
       conditioncheck_1_out_3, decoder3bit_1_out_5, decoder3bit_1_out_6, decoder3bit_1_out_7,
       decoder3bit_1_out_8, decoder3bit_1_out_9, decoder3bit_1_out_10, decoder3bit_1_out_11,
       decoder3bit_1_out_12, decoder3bit_2_out_5, decoder3bit_2_out_6, decoder3bit_2_out_7,
       decoder3bit_2_out_8, decoder3bit_2_out_9, decoder3bit_2_out_10, decoder3bit_2_out_11,
       decoder3bit_2_out_12, opdecode_1_out_2, opdecode_1_out_3, opdecode_1_out_4, opdecode_1_out_5,
       or_1_out, or_2_out, or_3_out, risingedge_1_out_2, risingedge_2_out_2;
  wire [7:0] adder_1_out, adder_2_out, math_1_dout, multiplexer_2_out, multiplexer_5_out, multiplexer_6_out,
       readtristate_1_readalways, readtristate_2_readalways, readtristate_3_readalways,
       readtristate_4_readalways, register_1_q, register_2_q, register_3_q, register_4_q, register_5_q,
       register_6_q, register_7_q, register_8_q, register_9_q, register_10_q;

  buf buffer_1 (buffer_1_out, buffer_2_out);
  buf buffer_2 (buffer_2_out, buffer_3_out);
  buf buffer_3 (buffer_3_out, buffer_4_out);
  buf buffer_4 (buffer_4_out, decoder3bit_2_out_12);
  RisingEdge risingedge_1 (.in_1(buffer_1_out), .out_2(risingedge_1_out_2));
  RAM #(.trigger("high")) ram_1 (.addr(out_2), .we(risingedge_1_out_2), .din(out_6), .dout(out_3));  // open: oe
  Multiplexer #(.width(8)) multiplexer_1 (.in0(register_1_q), .in1(adder_2_out), .out(out_2), .sel(risingedge_2_out_2));
  Multiplexer #(.width(8)) multiplexer_2 (
    .in0(adder_1_out), .in1(readtristate_1_readalways), .out(multiplexer_2_out));  // open: sel
  RisingEdge risingedge_2 (.in_1(or_1_out), .out_2(risingedge_2_out_2));
  buf buffer_5 (buffer_5_out, buffer_17_out);
  buf buffer_6 (buffer_6_out, risingedge_2_out_2);
  Register #(.trigger("falling")) register_1 (
    .D(multiplexer_2_out), .Q(register_1_q), .clk(clock_1_out), .clr(Reset));  // open: en
  Adder adder_1 (.a(register_1_q), .b(out_5), .out(adder_1_out));  // open: cin, cout
  Adder adder_2 (.a(8'h28), .b(readtristate_1_readalways), .out(adder_2_out));  // open: cin, cout
  buf buffer_7 (buffer_7_out, buffer_5_out);
  buf buffer_8 (buffer_8_out, buffer_7_out);
  buf buffer_9 (buffer_9_out, buffer_8_out);
  buf buffer_10 (buffer_10_out, buffer_9_out);
  buf buffer_11 (buffer_11_out, buffer_6_out);
  buf buffer_12 (buffer_12_out, buffer_11_out);
  buf buffer_13 (buffer_13_out, buffer_12_out);
  buf buffer_14 (buffer_14_out, buffer_13_out);
  Clock #(.highDuration(30), .lowDuration(30)) clock_1 (.out(clock_1_out));
  Multiplexer #(.width(8)) multiplexer_3 (.in0(8'h1), .in1({8{1'b0}}), .out(out_5), .sel(1'b0));
  or or_1 (or_1_out, decoder3bit_1_out_12, decoder3bit_2_out_12);
  Register #(.trigger("high")) register_2 (.D(out_3), .Q(register_2_q), .clk(buffer_16_out), .clr(Reset));  // open: en
  buf buffer_15 (buffer_15_out, buffer_10_out);
  buf buffer_16 (buffer_16_out, buffer_15_out);
  buf buffer_17 (buffer_17_out, buffer_14_out);
  buf buffer_18 (buffer_18_out, clock_1_out);
  buf buffer_19 (buffer_19_out, buffer_18_out);
  buf buffer_20 (buffer_20_out, buffer_19_out);
  buf buffer_21 (buffer_21_out, buffer_20_out);
  buf buffer_22 (buffer_22_out, buffer_35_out);
  buf buffer_23 (buffer_23_out, buffer_22_out);
  buf buffer_24 (buffer_24_out, buffer_23_out);
  buf buffer_25 (buffer_25_out, buffer_24_out);
  Register #(.trigger("falling")) register_3 (
    .D(out_3), .clk(buffer_39_out), .Q(register_3_q), .clr(Reset));  // open: en
  buf buffer_26 (buffer_26_out, buffer_21_out);
  buf buffer_27 (buffer_27_out, buffer_26_out);
  buf buffer_28 (buffer_28_out, buffer_27_out);
  buf buffer_29 (buffer_29_out, buffer_28_out);
  buf buffer_30 (buffer_30_out, buffer_25_out);
  buf buffer_31 (buffer_31_out, buffer_30_out);
  buf buffer_32 (buffer_32_out, buffer_31_out);
  buf buffer_33 (buffer_33_out, buffer_32_out);
  Decoder3Bit decoder3bit_1 (
    .in_1(register_3_q[3]), .in_2(register_3_q[4]), .in_3(register_3_q[5]), .enabled(opdecode_1_out_4),
    .out_5(decoder3bit_1_out_5), .out_6(decoder3bit_1_out_6), .out_7(decoder3bit_1_out_7),
    .out_8(decoder3bit_1_out_8), .out_9(decoder3bit_1_out_9), .out_10(decoder3bit_1_out_10),
    .out_11(decoder3bit_1_out_11), .out_12(decoder3bit_1_out_12));
  buf buffer_34 (buffer_34_out, buffer_29_out);
  buf buffer_35 (buffer_35_out, buffer_34_out);
  buf buffer_36 (buffer_36_out, buffer_33_out);
  buf buffer_37 (buffer_37_out, buffer_36_out);
  buf buffer_38 (buffer_38_out, buffer_37_out);
  buf buffer_39 (buffer_39_out, buffer_38_out);
  Decoder3Bit decoder3bit_2 (
    .in_1(register_3_q[0]), .in_2(register_3_q[1]), .in_3(register_3_q[2]), .enabled(opdecode_1_out_4),
    .out_5(decoder3bit_2_out_5), .out_6(decoder3bit_2_out_6), .out_7(decoder3bit_2_out_7),
    .out_8(decoder3bit_2_out_8), .out_9(decoder3bit_2_out_9), .out_10(decoder3bit_2_out_10),
    .out_11(decoder3bit_2_out_11), .out_12(decoder3bit_2_out_12));
  or or_2 (or_2_out, opdecode_1_out_3, decoder3bit_2_out_8);
  Multiplexer #(.width(8)) multiplexer_4 (.in1(register_2_q), .out(out_6), .sel(decoder3bit_1_out_12));  // open: in0
  or or_3 (or_3_out, opdecode_1_out_2, decoder3bit_2_out_5);
  Multiplexer #(.width(8)) multiplexer_5 (.in0(out_6), .in1(math_1_dout), .out(multiplexer_5_out));  // open: sel
  OPDecode opdecode_1 (
    .in_1(register_3_q), .out_2(opdecode_1_out_2), .out_3(opdecode_1_out_3), .out_4(opdecode_1_out_4),
    .out_5(opdecode_1_out_5));
  Multiplexer #(.width(8)) multiplexer_6 (.in0(out_6), .in1(register_3_q), .out(multiplexer_6_out));  // open: sel
  Register #(.trigger("high")) register_4 (
    .D(multiplexer_6_out), .en(or_3_out), .Q(register_4_q), .clk(buffer_42_out), .clr(Reset));
  Register #(.trigger("high")) register_5 (
    .D(out_6), .en(decoder3bit_2_out_6), .Q(register_5_q), .clk(buffer_42_out), .clr(Reset));
  Register #(.trigger("high")) register_6 (
    .D(out_6), .en(decoder3bit_2_out_7), .Q(register_6_q), .clk(buffer_42_out), .clr(Reset));
  Register #(.trigger("high")) register_7 (
    .D(multiplexer_5_out), .en(or_2_out), .Q(register_7_q), .clk(buffer_42_out), .clr(Reset));
  Register #(.trigger("high")) register_8 (
    .D(out_6), .en(decoder3bit_2_out_9), .Q(register_8_q), .clk(buffer_42_out), .clr(Reset));
  Register #(.trigger("high")) register_9 (
    .D(out_6), .en(decoder3bit_2_out_10), .Q(register_9_q), .clk(buffer_42_out), .clr(Reset));
  Register #(.trigger("high")) register_10 (
    .D(out_6), .en(decoder3bit_2_out_11), .Q(register_10_q), .clk(buffer_42_out), .clr(Reset));
  ReadTriState readtristate_1 (
    .data(register_4_q), .enable(decoder3bit_1_out_5), .ReadOut(out_6), .ReadAlways(readtristate_1_readalways));
  ReadTriState readtristate_2 (
    .data(register_5_q), .enable(decoder3bit_1_out_6), .ReadOut(out_6), .ReadAlways(readtristate_2_readalways));
  ReadTriState readtristate_3 (
    .data(register_6_q), .enable(decoder3bit_1_out_7), .ReadOut(out_6), .ReadAlways(readtristate_3_readalways));
  ReadTriState readtristate_4 (
    .data(register_7_q), .enable(decoder3bit_1_out_8), .ReadOut(out_6), .ReadAlways(readtristate_4_readalways));
  ReadTriState readtristate_5 (.data(register_8_q), .enable(decoder3bit_1_out_9), .ReadOut(out_6));  // open: ReadAlways
  ReadTriState readtristate_6 (
    .data(register_9_q), .enable(decoder3bit_1_out_10), .ReadOut(out_6));  // open: ReadAlways
  ReadTriState readtristate_7 (
    .data(register_10_q), .enable(decoder3bit_1_out_11), .ReadOut(out_6));  // open: ReadAlways
  ConditionCheck conditioncheck_1 (
    .Condition(register_3_q), .Data(readtristate_4_readalways), .out_3(conditioncheck_1_out_3));
  and and_1 (and_1_out, opdecode_1_out_5, conditioncheck_1_out_3);
  buf buffer_40 (buffer_40_out, clock_1_out);
  buf buffer_41 (buffer_41_out, buffer_40_out);
  buf buffer_42 (buffer_42_out, buffer_41_out);
  Math math_1 (
    .OP(register_3_q), .ARG0(readtristate_2_readalways), .ARG1(readtristate_3_readalways), .dout(math_1_dout));

  assign out_4 = out_3;
endmodule

module OPDecode (
  input  [7:0] in_1,
  output out_2,
  output out_3,
  output out_4,
  output out_5
);

  wire not_1_out, not_2_out;

  not not_1 (not_1_out, in_1[7]);
  not not_2 (not_2_out, in_1[6]);
  and and_1 (out_2, not_2_out, not_1_out);
  and and_2 (out_3, in_1[6], not_1_out);
  and and_3 (out_4, not_2_out, in_1[7]);
  and and_4 (out_5, in_1[6], in_1[7]);
endmodule

module ReadTriState (
  input  [7:0] data,
  input  enable,
  output [7:0] ReadOut,
  output [7:0] ReadAlways
);

  Multiplexer #(.width(8)) multiplexer_1 (.in1(data), .out(ReadOut), .sel(enable));  // open: in0

  assign ReadAlways = data;
endmodule

module Decoder3Bit (
  input  in_1,
  input  in_2,
  input  in_3,
  input  enabled,
  output out_5,
  output out_6,
  output out_7,
  output out_8,
  output out_9,
  output out_10,
  output out_11,
  output out_12
);

  wire and_1_out, and_2_out, and_3_out, and_4_out, and_5_out, and_6_out, and_7_out, and_8_out, not_1_out,
       not_2_out, not_3_out;

  not not_1 (not_1_out, in_3);
  not not_2 (not_2_out, in_2);
  not not_3 (not_3_out, in_1);
  and and_1 (and_1_out, not_3_out, not_2_out, not_1_out);
  and and_2 (and_2_out, in_1, not_2_out, not_1_out);
  and and_3 (and_3_out, not_3_out, in_2, not_1_out);
  and and_4 (and_4_out, in_1, in_2, not_1_out);
  and and_5 (and_5_out, not_3_out, not_2_out, in_3);
  and and_6 (and_6_out, in_1, not_2_out, in_3);
  and and_7 (and_7_out, not_3_out, in_2, in_3);
  and and_8 (and_8_out, in_1, in_2, in_3);
  and and_9 (out_5, and_1_out, enabled);
  and and_10 (out_6, and_2_out, enabled);
  and and_11 (out_7, and_3_out, enabled);
  and and_12 (out_8, and_4_out, enabled);
  and and_13 (out_9, and_5_out, enabled);
  and and_14 (out_10, and_6_out, enabled);
  and and_15 (out_11, and_7_out, enabled);
  and and_16 (out_12, and_8_out, enabled);
endmodule

module Andsmall (
  input  in_1,
  input  in_2,
  output out_3
);

  and and_1 (out_3, in_1, in_2);
endmodule

module Math (
  input  [7:0] OP,
  input  [7:0] ARG0,
  input  [7:0] ARG1,
  output [7:0] dout
);

  wire decoder3bit_1_out_5, decoder3bit_1_out_6, decoder3bit_1_out_7, decoder3bit_1_out_8,
       decoder3bit_1_out_9, decoder3bit_1_out_10, decoder3bit_1_out_11, decoder3bit_1_out_12;
  wire [7:0] adder_1_out, and_1_out, divider_1_out, multiplier_1_out, not_1_out, or_1_out, subtractor_1_out,
       xor_1_out;

  Decoder3Bit decoder3bit_1 (
    .in_1(OP[0]), .in_2(OP[1]), .in_3(OP[2]), .enabled(1'b1), .out_5(decoder3bit_1_out_5),
    .out_6(decoder3bit_1_out_6), .out_7(decoder3bit_1_out_7), .out_8(decoder3bit_1_out_8),
    .out_9(decoder3bit_1_out_9), .out_10(decoder3bit_1_out_10), .out_11(decoder3bit_1_out_11),
    .out_12(decoder3bit_1_out_12));
  assign xor_1_out = ARG0 ^ ARG1;  // XOR_Gate xor_1, 8 bits wide
  assign and_1_out = ARG0 & ARG1;  // AND_Gate and_1, 8 bits wide
  assign or_1_out = ARG0 | ARG1;  // OR_Gate or_1, 8 bits wide
  assign not_1_out = ~ARG0;  // NOT_Gate not_1, 8 bits wide
  Adder adder_1 (.a(ARG0), .b(ARG1), .out(adder_1_out));  // open: cin, cout
  Subtractor subtractor_1 (.a(ARG0), .b(ARG1), .out(subtractor_1_out));  // open: bin, bout
  Multiplier multiplier_1 (.a(ARG0), .b(ARG1), .out(multiplier_1_out));  // open: cin, cout
  Divider divider_1 (.a(ARG0), .b(ARG1), .out(divider_1_out));  // open: upper, rem
  Multiplexer #(.width(8)) multiplexer_1 (.in1(xor_1_out), .out(dout), .sel(decoder3bit_1_out_5));  // open: in0
  Multiplexer #(.width(8)) multiplexer_2 (.in1(and_1_out), .out(dout), .sel(decoder3bit_1_out_6));  // open: in0
  Multiplexer #(.width(8)) multiplexer_3 (.in1(or_1_out), .out(dout), .sel(decoder3bit_1_out_7));  // open: in0
  Multiplexer #(.width(8)) multiplexer_4 (.in1(not_1_out), .out(dout), .sel(decoder3bit_1_out_8));  // open: in0
  Multiplexer #(.width(8)) multiplexer_5 (.in1(adder_1_out), .out(dout), .sel(decoder3bit_1_out_9));  // open: in0
  Multiplexer #(.width(8)) multiplexer_6 (.in1(subtractor_1_out), .out(dout), .sel(decoder3bit_1_out_10));  // open: in0
  Multiplexer #(.width(8)) multiplexer_7 (.in1(multiplier_1_out), .out(dout), .sel(decoder3bit_1_out_11));  // open: in0
  Multiplexer #(.width(8)) multiplexer_8 (.in1(divider_1_out), .out(dout), .sel(decoder3bit_1_out_12));  // open: in0
endmodule

module DetectTri (
  input  [7:0] in_1,
  output out_2
);

  Multiplexer multiplexer_1 (.in0(1'b1), .in1(1'b1), .out(out_2), .sel(in_1[7]));
endmodule

module RisingEdge (
  input  in_1,
  output out_2
);

  wire not_1_out, not_2_out, not_3_out;

  not not_1 (not_1_out, in_1);
  not not_2 (not_2_out, not_1_out);
  not not_3 (not_3_out, not_2_out);
  and and_1 (out_2, not_3_out, in_1);
endmodule

module ConditionCheck (
  input  [7:0] Condition,
  input  [7:0] Data,
  output out_3
);

  wire and_1_out, and_2_out, and_3_out, and_4_out, and_5_out, and_6_out, and_7_out, and_8_out, and_9_out,
       nor_1_out, not_1_out, not_2_out, not_3_out, not_4_out, not_5_out, not_6_out, not_7_out, not_8_out,
       or_1_out;

  not not_1 (not_1_out, Data[7]);
  nor nor_1 (nor_1_out, Data[7], Data[6], Data[5], Data[4], Data[3], Data[2], Data[1], Data[0]);
  and and_1 (and_1_out, not_3_out, not_1_out);
  or or_1 (or_1_out, Data[7], nor_1_out);
  not not_2 (not_2_out, Condition[5]);
  not not_3 (not_3_out, nor_1_out);
  not not_4 (not_4_out, Condition[4]);
  not not_5 (not_5_out, Condition[3]);
  not not_6 (not_6_out, Condition[2]);
  not not_7 (not_7_out, Condition[1]);
  not not_8 (not_8_out, Condition[0]);
  Multiplexer multiplexer_1 (.in1(1'b1), .out(out_3), .sel(and_2_out));  // open: in0
  and and_2 (and_2_out, not_8_out, not_7_out, not_6_out, not_5_out, not_4_out, not_2_out);
  Multiplexer multiplexer_2 (.in1(1'b0), .out(out_3), .sel(and_3_out));  // open: in0
  and and_3 (and_3_out, Condition[0], not_7_out, not_6_out, not_5_out, not_4_out, not_2_out);
  and and_4 (and_4_out, not_8_out, Condition[1], not_6_out, not_5_out, not_4_out, not_2_out);
  Multiplexer multiplexer_3 (.in1(nor_1_out), .out(out_3), .sel(and_4_out));  // open: in0
  and and_5 (and_5_out, Condition[0], Condition[1], not_6_out, not_5_out, not_4_out, not_2_out);
  Multiplexer multiplexer_4 (.in1(not_3_out), .out(out_3), .sel(and_5_out));  // open: in0
  and and_6 (and_6_out, not_8_out, not_7_out, Condition[2], not_5_out, not_4_out, not_2_out);
  Multiplexer multiplexer_5 (.in1(and_1_out), .out(out_3), .sel(and_6_out));  // open: in0
  and and_7 (and_7_out, Condition[0], not_7_out, Condition[2], not_5_out, not_4_out, not_2_out);
  Multiplexer multiplexer_6 (.in1(Data[7]), .out(out_3), .sel(and_7_out));  // open: in0
  and and_8 (and_8_out, not_8_out, Condition[1], Condition[2], not_5_out, not_4_out, not_2_out);
  Multiplexer multiplexer_7 (.in1(not_1_out), .out(out_3), .sel(and_8_out));  // open: in0
  and and_9 (and_9_out, Condition[0], Condition[1], Condition[2], not_5_out, not_4_out, not_2_out);
  Multiplexer multiplexer_8 (.in1(or_1_out), .out(out_3), .sel(and_9_out));  // open: in0
endmodule
