// Logisim project yes.circ as structural Verilog: 6 circuits, main circuit main
module main (
  input  in_1,
  input  in_2,
  input  in_3,
  input  in_4,
  input  in_5,
  input  in_6,
  input  in_7,
  input  in_8,
  input  in_9,
  input  RESET,
  output [7:0] out_11
);

  wire AFO, ALO, and_1_out, and_2_out, and_3_out, and_4_out, and_5_out, BPI, BPO, clock_1_out,
       decode4bit_1_out_2, decode4bit_1_out_3, EI, HLT, II, IO, MAI, multiplexer_6_out, not_2_out, not_3_out,
       not_4_out, not_5_out, OO, or_1_out, or_2_out, or_3_out, or_4_out, PCC, PCI, PCO, RAI, RAO, RBI, RBO,
       RMI, RMO, SPC, SPI, SPO, SPQ, SUB;
  wire [4:0] alu_1_overflow;
  wire [7:0] alu_1_dout, BP_q, memaddr_q, multiplexer_1_out, pc_1_dout, RA_q, ram_1_dout, RB_q, register_1_q,
       rom_2_data, rom_2_data_2, sp_1_out_7;
  wire [10:10] rom_1_data;
  wire [11:0] ledbar_2_p1;
  wire [23:16] rom_2_data_3;

  ALU alu_1 (
    .sub(SUB), .A(RA_q), .B(RB_q), .dout(alu_1_dout), .overflow(alu_1_overflow[0]), .zero(alu_1_overflow[1]),
    .greater(alu_1_overflow[2]), .less(alu_1_overflow[3]), .equal(alu_1_overflow[4]));
  Register INSTR (.D(multiplexer_1_out), .en(II), .clk(or_1_out), .Q(ledbar_2_p1[11:4]), .clr(RESET));
  Register RA (.D(multiplexer_1_out), .en(RAI), .clk(or_1_out), .Q(RA_q), .clr(RESET));
  Register RB (.D(multiplexer_1_out), .en(RBI), .clk(or_1_out), .Q(RB_q), .clr(RESET));
  // LedBar #(.inputtype("row"), .matrixcols(4)) WORD: pin names not known; wires that end beside it: ledbar_2_p1[11:8]
  Multiplexer #(.width(8)) multiplexer_1 (.in1(alu_1_dout), .out(multiplexer_1_out), .sel(ALO));  // open: in0
  // LedBar #(.inputtype("row")) FLAGS: pin names not known; wires that end beside it: RBI, {3'b000, alu_1_overflow}
  // LedBar #(.inputtype("row"), .matrixcols(4)) DATA: pin names not known; wires that end beside it: ledbar_2_p1[7:4]
  // NOT_Gate not_1 has open pins: in=ledbar_2_p1[11], out=open
  not not_2 (not_2_out, ledbar_2_p1[10]);
  Multiplexer #(.width(8)) multiplexer_2 (.in1(RA_q), .out(multiplexer_1_out), .sel(RAO));  // open: in0
  Multiplexer #(.width(8)) multiplexer_3 (
    .in1({3'b000, alu_1_overflow}), .out(multiplexer_1_out), .sel(AFO));  // open: in0
  Multiplexer #(.width(8)) multiplexer_4 (.in1(RB_q), .out(multiplexer_1_out), .sel(RBO));  // open: in0
  Multiplexer #(.width(8)) multiplexer_5 (
    .in1({4'b0000, ledbar_2_p1[7:4]}), .out(multiplexer_1_out), .sel(IO));  // open: in0
  or or_1 (or_1_out, clock_1_out, HLT);
  not not_3 (not_3_out, or_1_out);
  or or_2 (or_2_out, RESET, EI);
  not not_4 (not_4_out, ledbar_2_p1[9]);
  not not_5 (not_5_out, ledbar_2_p1[8]);
  // LedBar #(.inputtype("row")) lebus: pin names not known; wires that end beside it: multiplexer_1_out
  // LedBar #(.inputtype("row")) ledbar_1: pin names not known; wires that end beside it: multiplexer_1_out, in_9
  Clock #(.highDuration(5), .lowDuration(5)) clock_1 (.out(clock_1_out));
  // LedBar #(.inputtype("row"), .matrixcols(4)) ledbar_2: pin names not known; wires that end beside it: ledbar_2_p1[3:0]
  counter4bit counter4bit_1 (.CLK(not_3_out), .RESET(or_2_out), .out_3(ledbar_2_p1[3:0]));
  decode4bit decode4bit_1 (
    .in_1(ledbar_2_p1[3:0]), .out_2(decode4bit_1_out_2), .out_3(decode4bit_1_out_3));  // open: out_4, out_5, out_6, out_7, out_8, out_9, out_10, out_11, out_12, out_13, out_14, out_15, out_16, out_17
  and and_1 (and_1_out, not_5_out, ledbar_2_p1[9], not_2_out, ledbar_2_p1[11]);
  and and_2 (and_2_out, not_2_out, ledbar_2_p1[9], ledbar_2_p1[8], ledbar_2_p1[11]);
  and and_3 (and_3_out, ledbar_2_p1[11], not_5_out, not_4_out, ledbar_2_p1[10]);
  and and_4 (and_4_out, ledbar_2_p1[8], not_4_out, ledbar_2_p1[10], ledbar_2_p1[11]);
  and and_5 (and_5_out, not_5_out, ledbar_2_p1[9], ledbar_2_p1[10], ledbar_2_p1[11]);
  // LedBar #(.inputtype("row"), .matrixcols(12)) ledbar_3: pin names not known; wires that end beside it: ledbar_2_p1
  ROM #(.addrWidth(12), .dataWidth(24)) rom_1 (
    .addr(ledbar_2_p1),
    .data({HLT, EI, OO, BPO, BPI, SPQ, SPC, SPO, SPI, IO, II, PCC, PCO, rom_1_data[10], SUB, AFO, ALO, RMO, RMI, MAI, RBO, RBI, RAO, RAI}));
  Register memaddr (.D(multiplexer_1_out), .en(MAI), .clk(or_1_out), .Q(memaddr_q), .clr(RESET));
  Register BP (.D(multiplexer_1_out), .en(BPI), .clk(or_1_out), .Q(BP_q), .clr(RESET));
  Register register_1 (.D(multiplexer_1_out), .en(OO), .clk(or_1_out), .Q(register_1_q), .clr(RESET));
  or or_3 (or_3_out, decode4bit_1_out_2, decode4bit_1_out_3);
  Multiplexer multiplexer_6 (.in1(alu_1_overflow[1]), .out(multiplexer_6_out), .sel(and_1_out));  // open: in0
  Multiplexer multiplexer_7 (.in1(alu_1_overflow[2]), .out(multiplexer_6_out), .sel(and_2_out));  // open: in0
  Multiplexer multiplexer_8 (.in1(alu_1_overflow[3]), .out(multiplexer_6_out), .sel(and_3_out));  // open: in0
  Multiplexer multiplexer_9 (.in1(alu_1_overflow[4]), .out(multiplexer_6_out), .sel(and_4_out));  // open: in0
  Multiplexer multiplexer_10 (.in1(alu_1_overflow[0]), .out(multiplexer_6_out), .sel(and_5_out));  // open: in0
  RAM #(.asyncread("true")) ram_1 (
    .addr(memaddr_q), .we(RMI), .oe(1'b1), .clk(or_1_out), .din(multiplexer_1_out), .dout(ram_1_dout));
  pc pc_1 (.COUNT(PCC), .JMP(PCI), .DIN(multiplexer_1_out), .CLK(or_1_out), .RESET(RESET), .DOUT(pc_1_dout));
  SP sp_1 (.DIN(multiplexer_1_out), .COUNT(SPC), .Q(SPQ), .SET(SPI), .CLK(or_1_out), .RESET(RESET), .out_7(sp_1_out_7));
  ROM #(.dataWidth(24)) rom_2 (.addr(register_1_q), .data({rom_2_data_3, rom_2_data_2, rom_2_data}));
  Pull_Resistor #(.pull(1)) pull_resistor_1 (.node(multiplexer_6_out));
  Multiplexer #(.width(8)) multiplexer_11 (.in1(pc_1_dout), .out(multiplexer_1_out), .sel(PCO));  // open: in0
  Multiplexer #(.width(8)) multiplexer_12 (.in1(sp_1_out_7), .out(multiplexer_1_out), .sel(SPO));  // open: in0
  Multiplexer #(.width(8)) multiplexer_13 (.in1(BP_q), .out(multiplexer_1_out), .sel(BPO));  // open: in0
  or or_4 (or_4_out, or_3_out, multiplexer_6_out);
  // LedBar #(.inputtype("row")) ledbar_4: pin names not known; wires that end beside it: ram_1_dout
  Multiplexer #(.width(8)) multiplexer_14 (.in1(ram_1_dout), .out(multiplexer_1_out), .sel(RMO));  // open: in0
  _7_Segment_Display u_7_segment_display_1 (
    .g(rom_2_data_3[16]), .f(rom_2_data_3[17]), .a(rom_2_data_3[18]), .b(rom_2_data_3[19]),
    .e(rom_2_data_3[20]), .d(rom_2_data_3[21]), .c(rom_2_data_3[22]), .dp(rom_2_data_3[23]));
  _7_Segment_Display u_7_segment_display_2 (
    .g(rom_2_data_2[0]), .f(rom_2_data_2[1]), .a(rom_2_data_2[2]), .b(rom_2_data_2[3]), .e(rom_2_data_2[4]),
    .d(rom_2_data_2[5]), .c(rom_2_data_2[6]), .dp(rom_2_data_2[7]));
  _7_Segment_Display u_7_segment_display_3 (
    .g(rom_2_data[0]), .f(rom_2_data[1]), .a(rom_2_data[2]), .b(rom_2_data[3]), .e(rom_2_data[4]),
    .d(rom_2_data[5]), .c(rom_2_data[6]), .dp(rom_2_data[7]));
  and and_6 (PCI, rom_1_data[10], or_4_out);
  _7_Segment_Display u_7_segment_display_4 (
    .g(in_1), .f(in_2), .a(in_3), .b(in_4), .e(in_5), .d(in_6), .c(in_7), .dp(in_8));

  assign out_11 = {in_8, in_7, in_6, in_5, in_4, in_3, in_2, in_1};

  // Notes on the sheet:
  //   xxxx0000 : PCO MAI
  //   xxxx0001 : RMO II PCC
  //   contents of rom_1 (hex, n*v repeats v):
  //   810 3040 4001 400000 12*0 810 3040 4001 400000 12*0 810 3040 4001 400000 12*0 810 3040 4001 400000
  //   12*0 810 3040 4001 400000 12*0 810 3040 4001 400000 12*0 810 3040 4001 400000 12*0 810 3040 4001
  //   400000 12*0 810 3040 4001 400000 12*0 810 3040 4001 400000 12*0 810 3040 4001 400000 12*0 810 3040
  //   4001 400000 12*0 810 3040 4001 400000 12*0 810 3040 4001 400000 12*0 810 3040 4001 400000 12*0 810
  //   3040 4001 400000 12*0 810 3040 4004 400000 12*0 810 3040 4004 400000 12*0 810 3040 4004 400000 12*0
  //   810 3040 4004 400000 12*0 810 3040 4004 400000 12*0 810 3040 4004 400000 12*0 810 3040 4004 400000
  //   12*0 810 3040 4004 400000 12*0 810 3040 4004 400000 12*0 810 3040 4004 400000 12*0 810 3040 4004
  //   400000 12*0 810 3040 4004 400000 12*0 810 3040 4004 400000 12*0 810 3040 4004 400000 12*0 810 3040
  //   4004 400000 12*0 810 3040 4004 400000 12*0 810 3040 81 400000 12*0 810 3040 281 400000 12*0 810 3040
  //   81 400000 12*0 810 3040 281 400000 12*0 810 3040 84 400000 12*0 810 3040 284 400000 12*0 810 3040 84
  //   400000 12*0 810 3040 284 400000 12*0 810 3040 8080 400000 12*0 810 3040 8280 400000 12*0 810 3040
  //   8080 400000 12*0 810 3040 8280 400000 12*0 810 3040 80080 400000 12*0 810 3040 80280 400000 12*0 810
  //   3040 80080 400000 12*0 810 3040 80280 400000 12*0 810 3040 3 400000 12*0 810 3040 6 400000 12*0 810
  //   3040 8002 400000 12*0 810 3040 80002 400000 12*0 810 3040 9 400000 12*0 810 3040 c 400000 12*0 810
  //   3040 8008 400000 12*0 810 3040 80008 400000 12*0 810 3040 10001 400000 12*0 810 3040 10004 400000
  //   12*0 810 3040 18000 400000 12*0 810 3040 90000 400000 12*0 810 3040 100001 400000 12*0 810 3040
  //   100004 400000 12*0 810 3040 108000 400000 12*0 810 3040 180000 400000 12*0 810 3040 12 41 400000
  //   11*0 810 3040 12 44 400000 11*0 810 3040 12 8040 400000 11*0 810 3040 12 80040 400000 11*0 810 3040
  //   18 41 400000 11*0 810 3040 18 44 400000 11*0 810 3040 18 8040 400000 11*0 810 3040 18 80040 400000
  //   11*0 810 3040 10010 41 400000 11*0 810 3040 10010 44 400000 11*0 810 3040 10010 8040 400000 11*0 810
  //   3040 10010 80040 400000 11*0 810 3040 100010 41 400000 11*0 810 3040 100010 44 400000 11*0 810 3040
  //   100010 8040 400000 11*0 810 3040 100010 80040 400000 11*0 810 3040 12 22 400000 11*0 810 3040 12 28
  //   400000 11*0 810 3040 12 10020 400000 11*0 810 3040 12 100020 400000 11*0 810 3040 18 22 400000 11*0
  //   810 3040 18 28 400000 11*0 810 3040 18 10020 400000 11*0 810 3040 18 100020 400000 11*0 810 3040
  //   10010 22 400000 11*0 810 3040 10010 28 400000 11*0 810 3040 10010 10020 400000 11*0 810 3040 10010
  //   100020 400000 11*0 810 3040 100010 22 400000 11*0 810 3040 100010 28 400000 11*0 810 3040 100010
  //   10020 400000 11*0 810 3040 100010 100020 400000 11*0 810 3040 200002 400000 12*0 810 3040 200002
  //   400000 12*0 810 3040 200002 400000 12*0 810 3040 200002 400000 12*0 810 3040 200008 400000 12*0 810
  //   3040 200008 400000 12*0 810 3040 200008 400000 12*0 810 3040 200008 400000 12*0 810 3040 210000
  //   400000 12*0 810 3040 210000 400000 12*0 810 3040 210000 400000 12*0 810 3040 210000 400000 12*0 810
  //   3040 300000 400000 12*0 810 3040 300000 400000 12*0 810 3040 300000 400000 12*0 810 3040 300000
  //   400000 12*0 810 3040 10010 20022 400000 11*0 810 3040 10010 20022 400000 11*0 810 3040 10010 20022
  //   400000 11*0 810 3040 10010 20022 400000 11*0 810 3040 10010 20028 400000 11*0 810 3040 10010 20028
  //   400000 11*0 810 3040 10010 20028 400000 11*0 810 3040 10010 20028 400000 11*0 810 3040 10010 30020
  //   400000 11*0 810 3040 10010 30020 400000 11*0 810 3040 10010 30020 400000 11*0 810 3040 10010 30020
  //   400000 11*0 810 3040 10010 120020 400000 11*0 810 3040 10010 120020 400000 11*0 810 3040 10010
  //   120020 400000 11*0 810 3040 10010 120020 400000 11*0 810 3040 60000 10010 41 400000 10*0 810 3040
  //   60000 10010 41 400000 10*0 810 3040 60000 10010 41 400000 10*0 810 3040 60000 10010 41 400000 10*0
  //   810 3040 60000 10010 44 400000 10*0 810 3040 60000 10010 44 400000 10*0 810 3040 60000 10010 44
  //   400000 10*0 810 3040 60000 10010 44 400000 10*0 810 3040 60000 10010 8040 400000 10*0 810 3040 60000
  //   10010 8040 400000 10*0 810 3040 60000 10010 8040 4000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
  //   contents of rom_2 (hex, n*v repeats v):
  //   7e 48 3d 6d 4b 67 77 4c 7f 6f 487e 4848 483d 486d 484b 4867 4877 484c 487f 486f 3d7e 3d48 3d3d 3d6d
  //   3d4b 3d67 3d77 3d4c 3d7f 3d6f 6d7e 6d48 6d3d 6d6d 6d4b 6d67 6d77 6d4c 6d7f 6d6f 4b7e 4b48 4b3d 4b6d
  //   4b4b 4b67 4b77 4b4c 4b7f 4b6f 677e 6748 673d 676d 674b 6767 6777 674c 677f 676f 777e 7748 773d 776d
  //   774b 7767 7777 774c 777f 776f 4c7e 4c48 4c3d 4c6d 4c4b 4c67 4c77 4c4c 4c7f 4c6f 7f7e 7f48 7f3d 7f6d
  //   7f4b 7f67 7f77 7f4c 7f7f 7f6f 6f7e 6f48 6f3d 6f6d 6f4b 6f67 6f77 6f4c 6f7f 6f6f 487e7e 487e48 487e3d
  //   487e6d 487e4b 487e67 487e77 487e4c 487e7f 487e6f 48487e 484848 48483d 48486d 48484b 484867 484877
  //   48484c 48487f 48486f 483d7e 483d48 483d3d 483d6d 483d4b 483d67 483d77 483d4c 483d7f 483d6f 486d7e
  //   486d48 486d3d 486d6d 486d4b 486d67 486d77 486d4c 486d7f 486d6f 484b7e 484b48 484b3d 484b6d 484b4b
  //   484b67 484b77 484b4c 484b7f 484b6f 48677e 486748 48673d 48676d 48674b 486767 486777 48674c 48677f
  //   48676f 48777e 487748 48773d 48776d 48774b 487767 487777 48774c 48777f 48776f 484c7e 484c48 484c3d
  //   484c6d 484c4b 484c67 484c77 484c4c 484c7f 484c6f 487f7e 487f48 487f3d 487f6d 487f4b 487f67 487f77
  //   487f4c 487f7f 487f6f 486f7e 486f48 486f3d 486f6d 486f4b 486f67 486f77 486f4c 486f7f 486f6f 3d7e7e
  //   3d7e48 3d7e3d 3d7e6d 3d7e4b 3d7e67 3d7e77 3d7e4c 3d7e7f 3d7e6f 3d487e 3d4848 3d483d 3d486d 3d484b
  //   3d4867 3d4877 3d484c 3d487f 3d486f 3d3d7e 3d3d48 3d3d3d 3d3d6d 3d3d4b 3d3d67 3d3d77 3d3d4c 3d3d7f
  //   3d3d6f 3d6d7e 3d6d48 3d6d3d 3d6d6d 3d6d4b 3d6d67 3d6d77 3d6d4c 3d6d7f 3d6d6f 3d4b7e 3d4b48 3d4b3d
  //   3d4b6d 3d4b4b 3d4b67 3d4b77 3d4b4c 3d4b7f 3d4b6f 3d677e 3d6748 3d673d 3d676d 3d674b 3d6767
  //   fib 11 70 80 74 24 80 64 70 0f 33 80 ec 70 02 90 f0
endmodule

module ALU (
  input  [7:0] A,
  input  [7:0] B,
  input  sub,
  output [7:0] dout,
  output overflow,
  output zero,
  output greater,
  output less,
  output equal
);

  wire not_1_out, not_2_out, not_3_out, subtractor_1_bout;
  wire [7:0] adder_1_out, subtractor_1_out;

  // LedBar #(.inputtype("row")) ledbar_1: pin names not known; wires that end beside it: dout
  Adder adder_1 (.a(A), .b(B), .out(adder_1_out), .cout(overflow));  // open: cin
  Subtractor subtractor_1 (.a(A), .b(B), .out(subtractor_1_out), .bout(subtractor_1_bout));  // open: bin
  nor nor_1 (zero, dout[0], dout[1], dout[2], dout[3], dout[4], dout[5], dout[6], dout[7]);
  nor nor_2 (equal, subtractor_1_out[0], subtractor_1_out[1], subtractor_1_out[2], subtractor_1_out[3], subtractor_1_out[4], subtractor_1_out[5], subtractor_1_out[6], subtractor_1_out[7]);
  Multiplexer #(.width(8)) multiplexer_1 (.in0(adder_1_out), .in1(subtractor_1_out), .out(dout), .sel(sub));
  not not_1 (not_1_out, subtractor_1_bout);
  and and_1 (greater, not_1_out, not_2_out);
  not not_2 (not_2_out, equal);
  and and_2 (less, subtractor_1_bout, not_3_out);
  not not_3 (not_3_out, equal);
endmodule

module pc (
  input  [7:0] DIN,
  input  COUNT,
  input  JMP,
  input  CLK,
  input  RESET,
  output [7:0] DOUT
);

  wire [7:0] adder_1_out, ledbar_1_p1, multiplexer_2_out;

  // LedBar #(.inputtype("row")) ledbar_1: pin names not known; wires that end beside it: ledbar_1_p1
  Multiplexer #(.width(8)) multiplexer_1 (.in0(multiplexer_2_out), .in1(DIN), .out(ledbar_1_p1), .sel(JMP));
  Multiplexer #(.width(8)) multiplexer_2 (.in0(DOUT), .in1(adder_1_out), .out(multiplexer_2_out), .sel(COUNT));
  Register register_1 (.D(ledbar_1_p1), .en(1'b1), .clk(CLK), .Q(DOUT), .clr(RESET));
  // LedBar #(.inputtype("row")) ledbar_2: pin names not known; wires that end beside it: DOUT
  Adder adder_1 (.a(DOUT), .b(8'h1), .out(adder_1_out));  // open: cin, cout
endmodule

module SP (
  input  [7:0] DIN,
  input  COUNT,
  input  Q,
  input  SET,
  input  CLK,
  input  RESET,
  output [7:0] out_7
);

  wire [7:0] adder_1_out, multiplexer_1_out, multiplexer_2_out, multiplexer_3_out, not_1_out, register_1_q,
       subtractor_1_out;

  assign not_1_out = ~DIN;  // NOT_Gate not_1, 8 bits wide
  Register register_1 (.D(multiplexer_2_out), .Q(register_1_q), .clk(CLK), .clr(RESET));  // open: en
  assign out_7 = ~register_1_q;  // NOT_Gate not_2, 8 bits wide
  Multiplexer #(.width(8)) multiplexer_1 (
    .in0(register_1_q), .in1(multiplexer_3_out), .out(multiplexer_1_out), .sel(COUNT));
  Multiplexer #(.width(8)) multiplexer_2 (.in0(multiplexer_1_out), .in1(not_1_out), .out(multiplexer_2_out), .sel(SET));
  Adder adder_1 (.a(register_1_q), .b(8'h1), .out(adder_1_out));  // open: cin, cout
  Multiplexer #(.width(8)) multiplexer_3 (.in0(adder_1_out), .in1(subtractor_1_out), .out(multiplexer_3_out), .sel(Q));
  Subtractor subtractor_1 (.a(register_1_q), .b(8'h1), .out(subtractor_1_out));  // open: bin, bout
endmodule

module counter4bit (
  input  CLK,
  input  RESET,
  output [3:0] out_3
);

  wire t_ff_1_qn, t_ff_2_qn, t_ff_3_qn;

  T_Flip_Flop t_ff_1 (.T(1'b1), .clk(CLK), .Q(out_3[0]), .Qn(t_ff_1_qn), .reset(RESET));  // open: preset
  T_Flip_Flop t_ff_2 (.T(t_ff_1_qn), .clk(t_ff_1_qn), .Q(out_3[1]), .Qn(t_ff_2_qn), .reset(RESET));  // open: preset
  T_Flip_Flop t_ff_3 (.T(t_ff_2_qn), .clk(t_ff_2_qn), .Q(out_3[2]), .Qn(t_ff_3_qn), .reset(RESET));  // open: preset
  T_Flip_Flop t_ff_4 (.T(t_ff_3_qn), .clk(t_ff_3_qn), .Q(out_3[3]), .reset(RESET));  // open: Qn, preset
endmodule

module decode4bit (
  input  [3:0] in_1,
  output out_2,
  output out_3,
  output out_4,
  output out_5,
  output out_6,
  output out_7,
  output out_8,
  output out_9,
  output out_10,
  output out_11,
  output out_12,
  output out_13,
  output out_14,
  output out_15,
  output out_16,
  output out_17
);

  ROM #(.addrWidth(4), .dataWidth(16)) rom_1 (
    .addr(in_1),
    .data({out_17, out_16, out_15, out_14, out_13, out_12, out_11, out_10, out_9, out_8, out_7, out_6, out_5, out_4, out_3, out_2}));

  // Notes on the sheet:
  //   contents of rom_1 (hex, n*v repeats v):
  //   1 2 4 8 10 20 40 80 100 200 400 800 1000 2000 4000 8000
endmodule
